// Digital circuit PDP8-X.dig as structural Verilog
module PDP8_X (
  input  clk
);

  wire AC2RAMD, AC_CK, add_1_c_o, add_2_c_o, AND, and_1_out, and_3_out, and_4_out, and_6_out, and_8_out,
       and_9_out, and_11_out, and_12_out, and_13_out, and_14_out, and_15_out, and_17_out, and_18_out,
       and_19_out, and_22_out, and_23_out, and_24_out, and_25_out, and_26_out, and_27_out, and_28_out,
       and_30_out, and_32_out, and_33_out, and_34_out, and_36_out, and_37_out, and_38_out, and_39_out,
       and_40_out, and_41_out, and_43_out, and_44_out, and_45_out, and_46_out, and_48_out, and_49_out,
       and_50_out, and_51_out, and_52_out, and_53_out, and_55_out, and_56_out, and_57_out, and_58_out,
       and_59_out, and_60_out, and_61_out, and_62_out, and_63_out, and_65_out, and_66_out, and_68_out,
       and_69_out, and_70_out, and_71_out, and_73_out, and_74_out, and_75_out, and_76_out, and_78_out,
       and_79_out, and_80_out, and_81_out, and_83_out, and_84_out, and_85_out, and_86_out, and_87_out,
       and_88_out, and_90_out, and_91_out, and_92_out, and_93_out, and_94_out, and_95_out, and_96_out,
       and_97_out, and_98_out, and_100_out, and_102_out, and_104_out, and_105_out, and_106_out, and_107_out,
       and_109_out, and_111_out, and_112_out, and_113_out, and_115_out, and_116_out, and_117_out,
       and_118_out, and_119_out, and_120_out, and_141_out, and_145_out, and_147_out, AUTOIND, BP_ENABLED_b,
       CK0, CK1, CK2, CK3, CK4, CK5, CK6, CK7, CK8, CK9, CLA, CLAx, CNT_AND, CNT_AND_I, CNT_AND_IA, CNT_DCA,
       CNT_DCA_I, CNT_DCA_IA, CNT_ISZ, CNT_ISZ_I, CNT_ISZ_IA, CNT_JMP, CNT_JMP_I, CNT_JMP_IA, CNT_JMS,
       CNT_JMS_I, CNT_JMS_IA, CNT_OPR1, CNT_OPR2, CNT_OPR3, CNT_TAD, CNT_TAD_I, CNT_TAD_IA, comparator_1_eq,
       comparator_2_eq, counter_1_o1, counter_1_o2, counter_1_o3, counter_1_o4, counter_1_o5, counter_1_o6,
       counter_1_o7, counter_1_o8, counter_1_o9, counter_1_o10, counter_1_o11, counter_1_o12, counter_1_o13,
       counter_1_o14, counter_1_o15, counter_1_o16, counter_1_o17, counter_1_o18, counter_1_o19,
       counter_1_o20, counter_1_o21, counter_1_o22, counter_1_o23, counter_1_o24, counter_1_o25,
       counter_1_o26, counter_1_o27, counter_1_o28, counter_1_o29, counter_1_o30, counter_1_o31,
       counter_1_o32, counter_2_ovf, d_ff_1_q, DATA_CK, DCA, demultiplexer_1_out_0, demultiplexer_1_out_1,
       demultiplexer_1_out_2, demultiplexer_1_out_3, demultiplexer_1_out_4, demultiplexer_1_out_5,
       demultiplexer_1_out_6, demultiplexer_1_out_7, demultiplexer_2_out_3, demultiplexer_2_out_7,
       demultiplexer_3_out_3, demultiplexer_3_out_7, demultiplexer_4_out_10, demultiplexer_4_out_11,
       demultiplexer_4_out_12, demultiplexer_4_out_13, demultiplexer_4_out_14, demultiplexer_4_out_15,
       demultiplexer_4_out_16, demultiplexer_4_out_17, demultiplexer_4_out_18, demultiplexer_4_out_19,
       demultiplexer_4_out_20, demultiplexer_4_out_21, demultiplexer_4_out_22, demultiplexer_4_out_23,
       demultiplexer_4_out_24, demultiplexer_4_out_25, demultiplexer_4_out_26, demultiplexer_4_out_27,
       demultiplexer_4_out_28, demultiplexer_4_out_29, demultiplexer_4_out_30, demultiplexer_4_out_31,
       demultiplexer_4_out_32, demultiplexer_4_out_33, demultiplexer_4_out_34, demultiplexer_4_out_35,
       demultiplexer_4_out_36, demultiplexer_4_out_37, demultiplexer_4_out_38, demultiplexer_4_out_39,
       demultiplexer_4_out_40, demultiplexer_4_out_41, demultiplexer_4_out_42, demultiplexer_4_out_43,
       demultiplexer_4_out_44, demultiplexer_4_out_45, demultiplexer_4_out_46, demultiplexer_4_out_47,
       demultiplexer_4_out_48, demultiplexer_4_out_49, demultiplexer_4_out_50, demultiplexer_4_out_51,
       demultiplexer_4_out_52, demultiplexer_4_out_53, demultiplexer_4_out_54, demultiplexer_4_out_55,
       demultiplexer_4_out_56, demultiplexer_4_out_57, demultiplexer_4_out_58, demultiplexer_4_out_59,
       demultiplexer_4_out_60, demultiplexer_4_out_61, demultiplexer_4_out_62, demultiplexer_4_out_63,
       demultiplexer_6_out_0, demultiplexer_6_out_1, driver_1_out, driver_23_out, driver_24_out,
       driver_56_out, driver_57_out, driver_58_out, driver_62_out, driver_63_out, driver_67_out,
       driver_68_out, driver_97_out, driver_98_out, driver_287_out, driver_288_out, driver_293_out,
       driver_311_out, driver_312_out, driver_313_out, driver_317_out, driver_318_out, driver_322_out,
       driver_323_out, driver_327_out, driver_328_out, driver_333_out, driver_338_out, driver_341_out,
       driver_342_out, driver_343_out, driver_347_out, driver_348_out, driver_349_out, driver_350_out,
       driver_351_out, driver_352_out, driver_353_out, driver_355_out, driver_356_out, driver_357_out,
       driver_362_out, driver_363_out, driver_368_out, driver_372_out, driver_373_out, driver_383_out,
       driver_386_out, driver_387_out, driver_388_out, driver_390_out, driver_391_out, driver_392_out,
       driver_396_out, driver_397_out, driver_398_out, driver_402_out, driver_403_out, driver_408_out,
       driver_412_out, driver_413_out, driver_418_out, driver_422_out, driver_423_out, driver_433_out,
       driver_436_out, driver_437_out, driver_438_out, driver_440_out, driver_441_out, driver_442_out,
       driver_446_out, driver_447_out, driver_448_out, driver_452_out, driver_453_out, driver_457_out,
       driver_458_out, driver_466_out, driver_467_out, driver_468_out, driver_472_out, driver_473_out,
       driver_477_out, driver_478_out, driver_482_out, driver_483_out, driver_505_out, FLAG_PRNRDY, H_out,
       HALT, HLT_ENABLED_b, i_cla, i_cll, i_cma, i_cml, i_hlt, i_iac, i_nop, i_osr, I_out, i_ral, i_rar,
       i_rtl, i_rtr, i_skp, i_sma, i_sna, i_snl, i_spa, i_sza, i_szl, INC2RAMD, INCZERO, IND, IND2INC,
       IND2PC, IND2RAMA, IND_CK, INST_KCC, INST_KCF, INST_KIE, INST_KRB, INST_KRS, INST_KSF, INST_TCF,
       INST_TFL, INST_TLS, INST_TPC, INST_TSF, INST_TSK, IOT, IOT_1x, IOT_2x, IOT_3x, IOT_4x, IOT_5, IOT_5x,
       IOT_6, IOT_6x, IOT_7, IOT_8, IOT_9, IOT_DEVCPU, IOT_DEVHSP, IOT_DEVHSR, IOT_DEVKBD, IOT_DEVPRI, IR2PC,
       IR2RAMA, IR_CK, ISZ, JMP, JMS, LD2INC, LINK, LINK_CK, monoflop_1_q, monoflop_2_q, monoflop_3_nq,
       monoflop_3_q, monoflop_4_q, monoflop_5_q, MP, MQ_CK, nand_1_out, NOIND, nor_1_out, nor_2_out,
       nor_3_out, nor_4_out, not_1_out, not_2_out, not_4_out, not_5_out, not_6_out, OPR, OPR1, OPR2, OPR3,
       OPR_ASL, OPR_CLA1, OPR_CLA2, OPR_CLA3, OPR_CLL, OPR_CMA, OPR_CML, OPR_DVI, OPR_HLT, OPR_IAC, OPR_LEFT,
       OPR_LSR, OPR_MQA, OPR_MQL, OPR_MUY, OPR_NA1, OPR_NMI, OPR_NOP, OPR_OPERATION, OPR_OSR, OPR_RIGHT,
       OPR_SCA, OPR_SCL, OPR_SHL, OPR_SMASPA, OPR_SNLSZL, OPR_SWP, OPR_SZASNA, OPR_TSTINV, OPR_X2, or_1_out,
       or_2_out, or_3_out, or_5_out, or_6_out, or_7_out, or_8_out, or_9_out, or_10_out, or_11_out, PC2ADDR,
       PC2RAMD, PC_CK, PC_eq_200, PC_LD, PH00, PH01, PH02, PH03, PH04, PH05, PH06, PH07, PH08, PH09, PH10,
       PH11, PH12, PH13, PH14, PH15, PH_FIRST, PH_LAST, PH_STB, R_out, RAM_OE, RAM_WE, RAMA_HOLD,
       RAMD2AC_ADD, RAMD2AC_AND, RAMD2IND, RAMD2PC, reset_1_out, ROT2AC, rotater_1_p5, rs_ff_as_1_q,
       rs_ff_as_2_q, S_out, SKIP, STB0, STB1, STB2, STB3, STB4, STB5, STB6, STB7, STB8, STB9, TAD, TAD_OVF_q,
       xor_1_out, xor_2_out, xor_3_out, xor_4_out, xor_5_out;
  wire [2:0] and_142_out, DA0, DA1, DA2, DA3, IND0, IND1, IND2, IND3, RA0, RA1, RA2, RA3;
  wire [3:0] CK_NUM;
  wire [4:0] counter_2_out;
  wire [11:0] AC, add_1_s, add_2_s, and_2_out, and_5_out, and_7_out, autocapture_1__10, autocapture_1__11,
       autocapture_1__12, autocapture_1__13, autocapture_1__14, autocapture_1__15, autocapture_1__16,
       autocapture_1__17, bitextender_1_out, bitextender_2_out, bitextender_3_out, BUS_IR, BUS_PC,
       dipswitch_1_out, driver_6_out, driver_14_out, driver_18_out, INC_s, LATCHED_PC, LATCHEDDATA, MQ,
       not_3_out, or_4_out, PCIN, RAMDATA, register_1_q, rotater_1_p4, xor_6_out;
  wire [31:0] COUNT_out, INSTRUCTION_COUNT_out;

  Comparator #(.Bits(12)) comparator_1 (.a({RA3, RA2, RA1, RA0}), .b(12'h5e), .eq(comparator_1_eq));  // open: gt, lt
  xor xor_1 (xor_1_out, CK0, PC_eq_200);
  and and_1 (and_1_out, comparator_1_eq, RAM_WE);
  assign driver_1_out = PC_eq_200 ? PC_eq_200 : 1'bz;  // Driver driver_1
  assign PC_LD = PC_eq_200 ? PC_eq_200 : 1'bz;  // Driver driver_2
  LED led_1 (.in(IR2PC));
  assign PCIN = PC_eq_200 ? 12'h80 : 12'bz;  // Driver driver_3
  COUNTER counter_1 (
    .i1(CNT_AND), .i2(CNT_AND_I), .i3(CNT_AND_IA), .i4(CNT_TAD), .i5(CNT_TAD_I), .i6(CNT_TAD_IA),
    .i7(CNT_ISZ), .i8(CNT_ISZ_I), .i9(CNT_ISZ_IA), .i10(CNT_DCA), .i11(CNT_DCA_I), .i12(CNT_DCA_IA),
    .i13(CNT_JMS), .i14(CNT_JMS_I), .i15(CNT_JMS_IA), .i16(CNT_JMP), .i17(CNT_JMP_I), .i18(CNT_JMP_IA),
    .i19(CNT_OPR1), .i20(CNT_OPR2), .i21(IOT_DEVCPU), .i22(IOT_DEVHSR), .i23(IOT_DEVHSP), .i24(IOT_DEVKBD),
    .i25(IOT_DEVPRI), .i26(IOT_5), .i27(IOT_6), .i28(IOT_7), .i29(IOT_8), .i30(IOT_9), .i31(IOT_1x),
    .i32(IOT_2x), .C(1'b0), .E(PH02), .o1(counter_1_o1), .o2(counter_1_o2), .o3(counter_1_o3),
    .o4(counter_1_o4), .o5(counter_1_o5), .o6(counter_1_o6), .o7(counter_1_o7), .o8(counter_1_o8),
    .o9(counter_1_o9), .o10(counter_1_o10), .o11(counter_1_o11), .o12(counter_1_o12), .o13(counter_1_o13),
    .o14(counter_1_o14), .o15(counter_1_o15), .o16(counter_1_o16), .o17(counter_1_o17), .o18(counter_1_o18),
    .o19(counter_1_o19), .o20(counter_1_o20), .o21(counter_1_o21), .o22(counter_1_o22), .o23(counter_1_o23),
    .o24(counter_1_o24), .o25(counter_1_o25), .o26(counter_1_o26), .o27(counter_1_o27), .o28(counter_1_o28),
    .o29(counter_1_o29), .o30(counter_1_o30), .o31(counter_1_o31), .o32(counter_1_o32));
  AUTOCAPTURE autocapture_1 (
    .D(RAMDATA), .A({RA3, RA2, RA1, RA0}), .WR(RAM_WE), ._10(autocapture_1__10), ._11(autocapture_1__11),
    ._12(autocapture_1__12), ._13(autocapture_1__13), ._14(autocapture_1__14), ._15(autocapture_1__15),
    ._16(autocapture_1__16), ._17(autocapture_1__17));
  Counter #(.Bits(32)) INSTRUCTION_COUNT (.en(1'b1), .C(CK0), .clr(1'b0), .out(INSTRUCTION_COUNT_out));  // open: ovf
  Register #(.Bits(12)) register_1 (.D(RAMDATA), .C(and_1_out), .en(1'b1), .Q(register_1_q));
  Register #(.Bits(12)) register_2 (.D(BUS_PC), .C(xor_1_out), .en(1'b1), .Q(LATCHED_PC));
  // OC12 oc12_1: pin names not known; wires that end beside it: BUS_IR[6:0], BUS_PC[11:7], MP, IR2PC, PCIN[6:0], PCIN[11:7], PCIN
  // Probe on counter_1_o1
  // Probe on counter_1_o2
  // Probe on counter_1_o3
  // Probe on counter_1_o4
  // Probe on counter_1_o5
  // Probe on counter_1_o6
  // Probe on counter_1_o7
  // Probe on counter_1_o8
  // Probe on counter_1_o9
  // Probe on counter_1_o10
  // Probe on counter_1_o11
  // Probe on counter_1_o12
  // Probe on counter_1_o13
  // Probe on counter_1_o14
  // Probe on counter_1_o15
  // Probe on counter_1_o16
  // Probe on counter_1_o17
  // Probe on counter_1_o18
  // Probe on counter_1_o19
  // Probe on counter_1_o20
  // Probe on counter_1_o21
  // Probe on counter_1_o22
  // Probe on counter_1_o23
  // Probe on counter_1_o24
  // Probe on counter_1_o25
  // Probe on counter_1_o26
  // Probe on counter_1_o27
  // Probe on counter_1_o28
  // Probe on counter_1_o29
  // Probe on counter_1_o30
  // Probe on counter_1_o31
  // Probe on counter_1_o32
  // Probe on autocapture_1__10
  // Probe on autocapture_1__11
  // Probe on autocapture_1__12
  // Probe on autocapture_1__13
  // Probe on autocapture_1__14
  // Probe on autocapture_1__15
  // Probe on autocapture_1__16
  // Probe on autocapture_1__17
  // Probe on INSTRUCTION_COUNT_out
  // Probe on register_1_q
  // Probe on PCIN
  LED led_2 (.in(PC_CK));
  LED led_3 (.in(RAMD2PC));
  assign PCIN = RAMD2PC ? {DA3, DA2, DA1, DA0} : 12'bz;  // Driver driver_4
  LED led_4 (.in(IND2PC));
  assign PCIN = IND2PC ? {IND3, IND2, IND1, IND0} : 12'bz;  // Driver driver_5
  LED led_5 (.in(LINK));
  // Probe on {DA3, DA2, DA1, DA0}
  xor xor_2 (xor_2_out, PC_CK, driver_1_out);
  Seven_Seg_Hex seven_seg_hex_1 (.d({1'b0, BUS_PC[11:9]}), .dp(1'b0));
  Seven_Seg_Hex seven_seg_hex_2 (.d({1'b0, BUS_IR[11:9]}), .dp(1'b0));
  Seven_Seg_Hex seven_seg_hex_3 (.d({1'b0, AC[11:9]}), .dp(1'b0));
  Seven_Seg_Hex seven_seg_hex_4 (.d({1'b0, MQ[11:9]}), .dp(1'b0));
  Seven_Seg_Hex seven_seg_hex_5 (.d({1'b0, IND3}), .dp(1'b0));
  Seven_Seg_Hex seven_seg_hex_6 (.d({1'b0, RA3}), .dp(1'b0));
  Seven_Seg_Hex seven_seg_hex_7 (.d({1'b0, RAMDATA[11:9]}), .dp(1'b0));
  Seven_Seg_Hex seven_seg_hex_8 (.d({1'b0, PCIN[11:9]}), .dp(1'b0));
  Seven_Seg_Hex seven_seg_hex_9 (.d({1'b0, DA3}), .dp(1'b0));
  not not_1 (not_1_out, xor_2_out);
  LED led_6 (.in(PC_LD));
  Seven_Seg_Hex seven_seg_hex_10 (.d({1'b0, BUS_PC[8:6]}), .dp(1'b0));
  Seven_Seg_Hex seven_seg_hex_11 (.d({1'b0, BUS_IR[8:6]}), .dp(1'b0));
  Seven_Seg_Hex seven_seg_hex_12 (.d({1'b0, AC[8:6]}), .dp(1'b0));
  Seven_Seg_Hex seven_seg_hex_13 (.d({1'b0, MQ[8:6]}), .dp(1'b0));
  Seven_Seg_Hex seven_seg_hex_14 (.d({1'b0, IND2}), .dp(1'b0));
  Seven_Seg_Hex seven_seg_hex_15 (.d({1'b0, RA2}), .dp(1'b0));
  Seven_Seg_Hex seven_seg_hex_16 (.d({1'b0, RAMDATA[8:6]}), .dp(1'b0));
  Seven_Seg_Hex seven_seg_hex_17 (.d({1'b0, PCIN[8:6]}), .dp(1'b0));
  Seven_Seg_Hex seven_seg_hex_18 (.d({1'b0, DA2}), .dp(1'b0));
  LED led_7 (.in(RAMD2AC_ADD));
  CounterPreset #(.Bits(12)) PC (
    .en(1'b1), .C(not_1_out), .dir(1'b0), .in(PCIN), .ld(PC_LD), .clr(reset_1_out), .out(BUS_PC));  // open: ovf
  Seven_Seg_Hex seven_seg_hex_19 (.d({1'b0, BUS_PC[5:3]}), .dp(1'b0));
  Seven_Seg_Hex seven_seg_hex_20 (.d({1'b0, BUS_IR[5:3]}), .dp(1'b0));
  Seven_Seg_Hex seven_seg_hex_21 (.d({1'b0, AC[5:3]}), .dp(1'b0));
  Seven_Seg_Hex seven_seg_hex_22 (.d({1'b0, MQ[5:3]}), .dp(1'b0));
  Seven_Seg_Hex seven_seg_hex_23 (.d({1'b0, IND1}), .dp(1'b0));
  Seven_Seg_Hex seven_seg_hex_24 (.d({1'b0, RA1}), .dp(1'b0));
  Seven_Seg_Hex seven_seg_hex_25 (.d({1'b0, RAMDATA[5:3]}), .dp(1'b0));
  Seven_Seg_Hex seven_seg_hex_26 (.d({1'b0, PCIN[5:3]}), .dp(1'b0));
  Seven_Seg_Hex seven_seg_hex_27 (.d({1'b0, DA1}), .dp(1'b0));
  assign and_2_out = AC & {DA3, DA2, DA1, DA0};  // And and_2, 12 bits wide
  Add #(.Bits(12)) add_1 (.a(AC), .b({DA3, DA2, DA1, DA0}), .c_i(1'b0), .s(add_1_s), .c_o(add_1_c_o));
  and and_3 (and_3_out, add_1_c_o, RAMD2AC_ADD);
  LED led_8 (.in(and_3_out));
  Reset #(.invertOutput("false")) reset_1 (.out(reset_1_out));
  Seven_Seg_Hex seven_seg_hex_28 (.d({1'b0, BUS_PC[2:0]}), .dp(1'b0));
  Seven_Seg_Hex seven_seg_hex_29 (.d({1'b0, BUS_IR[2:0]}), .dp(1'b0));
  Seven_Seg_Hex seven_seg_hex_30 (.d({1'b0, AC[2:0]}), .dp(1'b0));
  Seven_Seg_Hex seven_seg_hex_31 (.d({1'b0, MQ[2:0]}), .dp(1'b0));
  Seven_Seg_Hex seven_seg_hex_32 (.d({1'b0, IND0}), .dp(1'b0));
  Seven_Seg_Hex seven_seg_hex_33 (.d({1'b0, RA0}), .dp(1'b0));
  Seven_Seg_Hex seven_seg_hex_34 (.d({1'b0, RAMDATA[2:0]}), .dp(1'b0));
  Seven_Seg_Hex seven_seg_hex_35 (.d({1'b0, PCIN[2:0]}), .dp(1'b0));
  Seven_Seg_Hex seven_seg_hex_36 (.d({1'b0, DA0}), .dp(1'b0));
  // Probe on AC
  // Probe on and_2_out
  // Probe on add_1_s
  LED led_9 (.in(add_1_c_o));
  // Probe on rotater_1_p4
  D_FF TAD_OVF (.D(and_3_out), .C(STB1), .Q(TAD_OVF_q));  // open: nQ
  LED led_10 (.in(STB1));
  // Probe on BUS_PC
  and and_4 (and_4_out, OPR_MQL, MQ_CK);
  LED led_11 (.in(MQ_CK));
  LED led_12 (.in(TAD_OVF_q));
  // OC12 oc12_2: pin names not known; wires that end beside it: BUS_PC, BUS_IR[6:0], BUS_PC[11:7], MP, IR2RAMA, {RA2[0], RA1, RA0}, {RA3, RA2[2:1]}
  LED led_13 (.in(IR2RAMA));
  LED led_14 (.in(INST_KCF));
  LED led_15 (.in(i_nop));
  LED led_16 (.in(and_4_out));
  assign driver_6_out = RAMD2AC_AND ? and_2_out : 12'bz;  // Driver driver_6
  LED led_17 (.in(RAMD2AC_AND));
  assign driver_6_out = RAMD2AC_ADD ? add_1_s : 12'bz;  // Driver driver_7
  LED led_18 (.in(RAMD2AC_ADD));
  assign driver_6_out = ROT2AC ? rotater_1_p4 : 12'bz;  // Driver driver_8
  LED led_19 (.in(ROT2AC));
  xor xor_3 (xor_3_out, TAD_OVF_q, rotater_1_p5);
  LED led_20 (.in(PC2ADDR));
  assign {RA3, RA2, RA1, RA0} = PC2ADDR ? BUS_PC : 12'bz;  // Driver driver_9
  LED led_21 (.in(INST_KSF));
  LED led_22 (.in(i_cla));
  // Probe on and_5_out
  // Probe on driver_6_out
  LED led_23 (.in(xor_3_out));
  // Probe on {RA3, RA2, RA1, RA0}
  LED led_24 (.in(IND2RAMA));
  LED led_25 (.in(INST_KCC));
  LED led_26 (.in(INST_KRS));
  LED led_27 (.in(i_cll));
  Button S (.out(S_out));
  Button I (.out(I_out));
  Button R (.out(R_out));
  Button H (.out(H_out));
  Button P (.out(PC_eq_200));
  assign and_5_out = AC & ~bitextender_1_out;  // And and_5, 12 bits wide
  LED led_28 (.in(AC_CK));
  D_FF u_LINK (.D(xor_3_out), .C(LINK_CK), .Q(LINK));  // open: nQ
  LED led_29 (.in(LINK_CK));
  LED led_30 (.in(RAM_WE));
  LED led_31 (.in(RAM_OE));
  assign {RA3, RA2, RA1, RA0} = IND2RAMA ? {IND3, IND2, IND1, IND0} : 12'bz;  // Driver driver_10
  LED led_32 (.in(INST_KIE));
  LED led_33 (.in(i_cma));
  LED led_34 (.in(AND));
  Monoflop #(.timerDelay(2)) monoflop_1 (.C(I_out), .R(1'b0), .Q(monoflop_1_q));  // open: nQ
  Monoflop monoflop_2 (.C(R_out), .R(1'b0), .Q(monoflop_2_q));  // open: nQ
  D_FF #(.Bits(12)) u_MQ (.D(and_5_out), .C(and_4_out), .Q(MQ));  // open: nQ
  D_FF #(.Bits(12)) u_AC (.D(driver_6_out), .C(AC_CK), .Q(AC));  // open: nQ
  or or_1 (or_1_out, OPR_CLA1, OPR_CLA2, OPR_CLA3, OPR_MQL);
  LED led_35 (.in(LINK));
  EEPROM #(.AddrBits(12), .isProgramMemory("true"), .Bits(12)) eeprom_1 (
    .A({RA3, RA2, RA1, RA0}), .CS(1'b1), .WE(RAM_WE), .OE(RAM_OE), .D(RAMDATA));
  LED led_36 (.in(INST_KRB));
  LED led_37 (.in(i_cml));
  LED led_38 (.in(TAD));
  LED led_39 (.in(ISZ));
  Comparator #(.Bits(12)) comparator_2 (.a(BUS_PC), .b(12'hac7), .eq(comparator_2_eq));  // open: gt, lt
  // Probe on MQ
  BitExtender #(.inputBits(1), .outputBits(12)) bitextender_1 (.in(OPR_CLA3), .out(bitextender_1_out));
  // Probe on AC
  BitExtender #(.inputBits(1), .outputBits(12)) bitextender_2 (.in(or_1_out), .out(bitextender_2_out));
  LED led_40 (.in(or_1_out));
  and and_6 (and_6_out, LINK, ~OPR_CLL);  // And
  LED led_41 (.in(OPR_CLL));
  // Probe on RAMDATA
  LED led_42 (.in(INST_TFL));
  LED led_43 (.in(i_iac));
  LED led_44 (.in(DCA));
  Switch #(.Closed("true")) HLT_ENABLED (.A(HALT), .B(HLT_ENABLED_b));
  assign and_7_out = AC & ~bitextender_2_out;  // And and_7, 12 bits wide
  LED led_45 (.in(and_6_out));
  assign {DA3, DA2, DA1, DA0} = RAM_OE ? RAMDATA : 12'bz;  // Driver driver_11
  assign RAMDATA = RAM_WE ? {DA3, DA2, DA1, DA0} : 12'bz;  // Driver driver_12
  LED led_46 (.in(INST_TSF));
  LED led_47 (.in(i_rar));
  LED led_48 (.in(i_rtr));
  LED led_49 (.in(JMS));
  RS_FF_AS rs_ff_as_1 (.S(monoflop_2_q), .R(or_3_out), .Q(rs_ff_as_1_q));  // open: nQ
  PullDown pulldown_1 (.out(HLT_ENABLED_b));
  Switch #(.Closed("true")) BP_ENABLED (.A(comparator_2_eq), .B(BP_ENABLED_b));
  // Probe on and_7_out
  LED led_50 (.in(OPR_CML));
  LED led_51 (.in(PC2RAMD));
  assign {DA3, DA2, DA1, DA0} = PC2RAMD ? BUS_PC : 12'bz;  // Driver driver_13
  LED led_52 (.in(INST_TCF));
  LED led_53 (.in(i_ral));
  LED led_54 (.in(JMP));
  LED led_55 (.in(IOT));
  or or_2 (or_2_out, monoflop_1_q, monoflop_2_q, rs_ff_as_1_q);
  or or_3 (or_3_out, H_out, BP_ENABLED_b, HLT_ENABLED_b);
  PullDown pulldown_2 (.out(BP_ENABLED_b));
  assign driver_14_out = OPR_MQA ? MQ : 12'bz;  // Driver driver_14
  LED led_56 (.in(OPR_MQA));
  xor xor_4 (xor_4_out, and_6_out, OPR_CML);
  // Probe on {DA3, DA2, DA1, DA0}
  LED led_57 (.in(INC2RAMD));
  assign {DA3, DA2, DA1, DA0} = INC2RAMD ? INC_s : 12'bz;  // Driver driver_15
  LED led_58 (.in(AC2RAMD));
  assign {DA3, DA2, DA1, DA0} = AC2RAMD ? AC : 12'bz;  // Driver driver_16
  LED led_59 (.in(INST_TPC));
  LED led_60 (.in(INST_TSK));
  LED led_61 (.in(i_rtl));
  LED led_62 (.in(OPR));
  LED led_63 (.in(or_2_out));
  LED led_64 (.in(or_3_out));
  assign driver_14_out = OPR_OSR ? not_3_out : 12'bz;  // Driver driver_17
  LED led_65 (.in(OPR_OSR));
  // Probe on driver_14_out
  assign or_4_out = driver_14_out | and_7_out;  // Or or_4, 12 bits wide
  BitExtender #(.inputBits(1), .outputBits(12)) bitextender_3 (.in(OPR_CMA), .out(bitextender_3_out));
  LED led_66 (.in(OPR_CMA));
  LED led_67 (.in(xor_4_out));
  not not_2 (not_2_out, IR_CK);
  LED led_68 (.in(IR_CK));
  LED led_69 (.in(INST_TLS));
  LED led_70 (.in(i_skp));
  LED led_71 (.in(NOIND));
  D_FF d_ff_1 (.D(counter_2_ovf), .C(clk), .Q(d_ff_1_q));  // open: nQ
  // Probe on or_4_out
  xor xor_5 (xor_5_out, and_9_out, xor_4_out);
  // TRANSP_LATCH IR: pin names not known; wires that end beside it: {DA3, DA2, DA1, DA0}, {DA3, DA2, DA1, DA0}, not_2_out, BUS_IR, BUS_IR
  LED led_72 (.in(i_sza));
  LED led_73 (.in(i_sma));
  LED led_74 (.in(IND));
  RS_FF_AS rs_ff_as_2 (.S(or_2_out), .R(d_ff_1_q), .Q(rs_ff_as_2_q));  // open: nQ
  // Probe on not_3_out
  assign xor_6_out = or_4_out ^ bitextender_3_out;  // XOr xor_6, 12 bits wide
  LED led_75 (.in(xor_5_out));
  // Probe on BUS_IR
  LED led_76 (.in(i_spa));
  LED led_77 (.in(AUTOIND));
  and and_8 (and_8_out, rs_ff_as_2_q, clk);
  // Probe on xor_6_out
  LED led_78 (.in(OPR_IAC));
  D_FF #(.Bits(12)) u_IND (.D({DA3, DA2, DA1, DA0}), .C(IND_CK), .Q({IND3, IND2, IND1, IND0}));  // open: nQ
  LED led_79 (.in(IND_CK));
  LED led_80 (.in(i_sna));
  LED led_81 (.in(MP));
  assign not_3_out = ~dipswitch_1_out;  // Not not_3, 12 bits wide
  Add #(.Bits(12)) add_2 (.a(xor_6_out), .b({12{1'b0}}), .c_i(OPR_IAC), .s(add_2_s), .c_o(add_2_c_o));
  LED led_82 (.in(i_szl));
  LED led_83 (.in(i_snl));
  or or_5 (or_5_out, S_out, and_8_out);
  LED led_84 (.in(or_5_out));
  DipSwitch dipswitch_1 (.out(dipswitch_1_out[11]));
  DipSwitch dipswitch_2 (.out(dipswitch_1_out[10]));
  DipSwitch dipswitch_3 (.out(dipswitch_1_out[9]));
  // Probe on add_2_s
  and and_9 (and_9_out, add_2_c_o, OPR_IAC);
  LED led_85 (.in(add_2_c_o));
  // Probe on {IND3, IND2, IND1, IND0}
  LED led_86 (.in(DATA_CK));
  LED led_87 (.in(i_osr));
  Counter #(.Bits(5)) counter_2 (
    .en(1'b1), .C(or_5_out), .clr(counter_2_ovf), .out(counter_2_out), .ovf(counter_2_ovf));
  PullDown pulldown_3 (.out(counter_2_ovf));
  DipSwitch dipswitch_4 (.out(dipswitch_1_out[8]));
  DipSwitch dipswitch_5 (.out(dipswitch_1_out[7]));
  DipSwitch dipswitch_6 (.out(dipswitch_1_out[6]));
  LED led_88 (.in(and_9_out));
  D_FF #(.Bits(12)) DATA (.D({DA3, DA2, DA1, DA0}), .C(DATA_CK), .Q(LATCHEDDATA));  // open: nQ
  LED led_89 (.in(i_hlt));
  DipSwitch dipswitch_7 (.out(dipswitch_1_out[5]));
  DipSwitch dipswitch_8 (.out(dipswitch_1_out[4]));
  DipSwitch dipswitch_9 (.out(dipswitch_1_out[3]));
  // Probe on LATCHEDDATA
  SEQUENCER sequencer_1 (
    .PH_FIRST(PH_FIRST), .PH_STB(PH_STB), .PH_LAST(PH_LAST),
    .STB_bits({STB9, STB8, STB7, STB6, STB5, STB4, STB3, STB2, STB1, STB0}),
    .CK_bits({CK9, CK8, CK7, CK6, CK5, CK4, CK3, CK2, CK1, CK0}), .CK_num(CK_NUM), .IN(counter_2_out));
  DipSwitch dipswitch_10 (.out(dipswitch_1_out[2]));
  DipSwitch dipswitch_11 (.out(dipswitch_1_out[1]));
  DipSwitch dipswitch_12 (.out(dipswitch_1_out[0]));
  // ROTATER rotater_1: pin names not known; wires that end beside it: {OPR_RIGHT, OPR_LEFT, OPR_X2}, add_2_s, xor_5_out, rotater_1_p4, rotater_1_p5
  LED led_90 (.in(IND2INC));
  assign driver_18_out = IND2INC ? {IND3, IND2, IND1, IND0} : 12'bz;  // Driver driver_18
  LED led_91 (.in(LD2INC));
  assign driver_18_out = LD2INC ? LATCHEDDATA : 12'bz;  // Driver driver_19
  // Probe on rotater_1_p4
  Seven_Seg_Hex seven_seg_hex_37 (.d(CK_NUM), .dp(1'b0));
  LED led_92 (.in(PH_FIRST));
  LED led_93 (.in(PH_STB));
  // Probe on driver_18_out
  Decoder #(.Selector_Bits(4)) decoder_1 (
    .sel(4'b1111), .out_0(PH00), .out_1(PH01), .out_2(PH02), .out_3(PH03), .out_4(PH04), .out_5(PH05),
    .out_6(PH06), .out_7(PH07), .out_8(PH08), .out_9(PH09), .out_10(PH10), .out_11(PH11), .out_12(PH12),
    .out_13(PH13), .out_14(PH14), .out_15(PH15));
  Seven_Seg_Hex seven_seg_hex_38 (.d(CK_NUM), .dp(1'b0));
  LED led_94 (.in(PH_FIRST));
  LED led_95 (.in(PH_STB));
  Seven_Seg_Hex seven_seg_hex_39 (.d(CK_NUM), .dp(1'b0));
  LED led_96 (.in(PH_LAST));
  // Probe on INC_s
  Add #(.Bits(12)) INC (.a({12{1'b0}}), .b(driver_18_out), .c_i(1'b1), .s(INC_s), .c_o(INCZERO));
  LED led_97 (.in(PH_LAST));
  // Probe on LATCHED_PC
  LED led_98 (.in(PH_FIRST));
  LED led_99 (.in(PH_STB));
  LED led_100 (.in(PH_LAST));
  and and_10 (CNT_AND, AND, NOIND, CK1);
  LED led_101 (.in(CNT_AND));
  and and_11 (and_11_out, AND, NOIND, STB1);
  LED led_102 (.in(and_11_out));
  and and_12 (and_12_out, CK0, 1'b1, 1'b1);
  assign IR2RAMA = CNT_AND ? CNT_AND : 1'bz;  // Driver driver_20
  assign RAMD2AC_AND = CNT_AND ? CNT_AND : 1'bz;  // Driver driver_21
  assign RAM_OE = CNT_AND ? CNT_AND : 1'bz;  // Driver driver_22
  assign driver_23_out = CNT_AND ? CNT_AND : 1'bz;  // Driver driver_23
  assign driver_24_out = CNT_AND ? CNT_AND : 1'bz;  // Driver driver_24
  Driver driver_25 (.in(and_11_out), .en(and_11_out));  // open: out
  Driver driver_26 (.in(and_11_out), .en(and_11_out));  // open: out
  Driver driver_27 (.in(and_11_out), .en(and_11_out));  // open: out
  assign AC_CK = and_11_out ? and_11_out : 1'bz;  // Driver driver_28
  Driver driver_29 (.in(and_11_out), .en(and_11_out));  // open: out
  LED led_103 (.in(and_12_out));
  nor nor_1 (nor_1_out, AC[0], AC[1], AC[2], AC[3], AC[4], AC[5], AC[6], AC[7], AC[8], AC[9], AC[10], AC[11]);
  assign PC2ADDR = and_12_out ? and_12_out : 1'bz;  // Driver driver_30
  assign RAM_OE = and_12_out ? and_12_out : 1'bz;  // Driver driver_31
  assign IR_CK = and_12_out ? and_12_out : 1'bz;  // Driver driver_32
  assign PC_CK = and_12_out ? and_12_out : 1'bz;  // Driver driver_33
  LED led_104 (.in(nor_1_out));
  and and_13 (and_13_out, nor_1_out, OPR_SZASNA);
  and and_14 (and_14_out, AC[11], OPR_SMASPA);
  and and_15 (and_15_out, LINK, OPR_SNLSZL);
  and and_16 (CNT_AND_I, AND, IND, PH02);
  and and_17 (and_17_out, AND, IND, PH03);
  and and_18 (and_18_out, AND, IND, PH04);
  and and_19 (and_19_out, AND, IND, PH05);
  LED led_105 (.in(and_13_out));
  or or_6 (or_6_out, and_13_out, and_14_out, and_15_out);
  LED led_106 (.in(and_14_out));
  LED led_107 (.in(and_15_out));
  and and_20 (HALT, OPR_HLT, CK1);
  assign IR2RAMA = CNT_AND_I ? CNT_AND_I : 1'bz;  // Driver driver_34
  LED led_108 (.in(CNT_AND_I));
  assign RAMD2IND = CNT_AND_I ? CNT_AND_I : 1'bz;  // Driver driver_35
  assign RAM_OE = CNT_AND_I ? CNT_AND_I : 1'bz;  // Driver driver_36
  Driver driver_37 (.in(CNT_AND_I), .en(CNT_AND_I));  // open: out
  Driver driver_38 (.in(CNT_AND_I), .en(CNT_AND_I));  // open: out
  assign IR2RAMA = and_17_out ? and_17_out : 1'bz;  // Driver driver_39
  LED led_109 (.in(and_17_out));
  assign RAMD2IND = and_17_out ? and_17_out : 1'bz;  // Driver driver_40
  assign RAM_OE = and_17_out ? and_17_out : 1'bz;  // Driver driver_41
  assign IND_CK = and_17_out ? and_17_out : 1'bz;  // Driver driver_42
  Driver driver_43 (.in(and_17_out), .en(and_17_out));  // open: out
  assign IND2RAMA = and_18_out ? and_18_out : 1'bz;  // Driver driver_44
  LED led_110 (.in(and_18_out));
  assign RAMD2AC_AND = and_18_out ? and_18_out : 1'bz;  // Driver driver_45
  assign RAM_OE = and_18_out ? and_18_out : 1'bz;  // Driver driver_46
  Driver driver_47 (.in(and_18_out), .en(and_18_out));  // open: out
  Driver driver_48 (.in(and_18_out), .en(and_18_out));  // open: out
  assign IND2RAMA = and_19_out ? and_19_out : 1'bz;  // Driver driver_49
  LED led_111 (.in(and_19_out));
  assign RAMD2AC_AND = and_19_out ? and_19_out : 1'bz;  // Driver driver_50
  assign RAM_OE = and_19_out ? and_19_out : 1'bz;  // Driver driver_51
  assign AC_CK = and_19_out ? and_19_out : 1'bz;  // Driver driver_52
  Driver driver_53 (.in(and_19_out), .en(and_19_out));  // open: out
  LED led_112 (.in(or_6_out));
  LED led_113 (.in(HALT));
  xor xor_7 (SKIP, or_6_out, OPR_TSTINV);
  LED led_114 (.in(SKIP));
  or or_7 (or_7_out, OPR_SNLSZL, OPR_SZASNA, OPR_SMASPA);
  LED led_115 (.in(or_7_out));
  and and_21 (CNT_AND_IA, AND, AUTOIND, PH02);
  and and_22 (and_22_out, AND, AUTOIND, PH03);
  and and_23 (and_23_out, AND, AUTOIND, PH04);
  and and_24 (and_24_out, AND, AUTOIND, PH05);
  and and_25 (and_25_out, AND, AUTOIND, PH06);
  and and_26 (and_26_out, AND, AUTOIND, PH07);
  and and_27 (and_27_out, AND, AUTOIND, PH08);
  LED led_116 (.in(CNT_AND_IA));
  LED led_117 (.in(and_22_out));
  LED led_118 (.in(and_23_out));
  LED led_119 (.in(and_24_out));
  LED led_120 (.in(and_25_out));
  LED led_121 (.in(and_26_out));
  LED led_122 (.in(and_27_out));
  assign IR2RAMA = CNT_AND_IA ? CNT_AND_IA : 1'bz;  // Driver driver_54
  assign RAM_OE = CNT_AND_IA ? CNT_AND_IA : 1'bz;  // Driver driver_55
  assign driver_56_out = CNT_AND_IA ? CNT_AND_IA : 1'bz;  // Driver driver_56
  assign driver_57_out = CNT_AND_IA ? CNT_AND_IA : 1'bz;  // Driver driver_57
  assign driver_58_out = CNT_AND_IA ? CNT_AND_IA : 1'bz;  // Driver driver_58
  assign IR2RAMA = and_22_out ? and_22_out : 1'bz;  // Driver driver_59
  assign IND_CK = and_22_out ? and_22_out : 1'bz;  // Driver driver_60
  assign RAM_OE = and_22_out ? and_22_out : 1'bz;  // Driver driver_61
  assign driver_62_out = and_22_out ? and_22_out : 1'bz;  // Driver driver_62
  assign driver_63_out = and_22_out ? and_22_out : 1'bz;  // Driver driver_63
  assign INC2RAMD = and_23_out ? and_23_out : 1'bz;  // Driver driver_64
  assign RAM_WE = and_23_out ? and_23_out : 1'bz;  // Driver driver_65
  assign IND2INC = and_23_out ? and_23_out : 1'bz;  // Driver driver_66
  assign driver_67_out = and_23_out ? and_23_out : 1'bz;  // Driver driver_67
  assign driver_68_out = and_23_out ? and_23_out : 1'bz;  // Driver driver_68
  assign IR2RAMA = and_24_out ? and_24_out : 1'bz;  // Driver driver_69
  assign RAMD2IND = and_24_out ? and_24_out : 1'bz;  // Driver driver_70
  assign RAM_OE = and_24_out ? and_24_out : 1'bz;  // Driver driver_71
  Driver driver_72 (.in(and_24_out), .en(and_24_out));  // open: out
  Driver driver_73 (.in(and_24_out), .en(and_24_out));  // open: out
  assign IR2RAMA = and_25_out ? and_25_out : 1'bz;  // Driver driver_74
  assign RAMD2IND = and_25_out ? and_25_out : 1'bz;  // Driver driver_75
  assign RAM_OE = and_25_out ? and_25_out : 1'bz;  // Driver driver_76
  assign IND_CK = and_25_out ? and_25_out : 1'bz;  // Driver driver_77
  Driver driver_78 (.in(and_25_out), .en(and_25_out));  // open: out
  assign IND2RAMA = and_26_out ? and_26_out : 1'bz;  // Driver driver_79
  assign RAMD2AC_AND = and_26_out ? and_26_out : 1'bz;  // Driver driver_80
  assign RAM_OE = and_26_out ? and_26_out : 1'bz;  // Driver driver_81
  Driver driver_82 (.in(and_26_out), .en(and_26_out));  // open: out
  Driver driver_83 (.in(and_26_out), .en(and_26_out));  // open: out
  assign IND2RAMA = and_27_out ? and_27_out : 1'bz;  // Driver driver_84
  assign RAMD2AC_AND = and_27_out ? and_27_out : 1'bz;  // Driver driver_85
  assign RAM_OE = and_27_out ? and_27_out : 1'bz;  // Driver driver_86
  assign AC_CK = and_27_out ? and_27_out : 1'bz;  // Driver driver_87
  Driver driver_88 (.in(and_27_out), .en(and_27_out));  // open: out
  or or_8 (or_8_out, INST_TPC, INST_TLS);
  and and_28 (and_28_out, INST_TSF, FLAG_PRNRDY, PH04);
  Monoflop #(.timerDelay(300)) monoflop_3 (.C(or_8_out), .R(1'b0), .Q(monoflop_3_q), .nQ(monoflop_3_nq));
  LED led_123 (.in(and_28_out));
  Counter #(.Bits(32)) COUNT (.en(1'b1), .C(or_8_out), .clr(1'b0), .out(COUNT_out));  // open: ovf
  Terminal #(.termWidth(20), .termHeight(10)) PRN (.D(AC[7:0]), .C(or_8_out), .en(1'b1));
  assign IR_CK = and_28_out ? and_28_out : 1'bz;  // Driver driver_89
  assign PC_CK = and_28_out ? and_28_out : 1'bz;  // Driver driver_90
  Driver driver_91 (.in(and_28_out), .en(and_28_out));  // open: out
  Driver driver_92 (.in(and_28_out), .en(and_28_out));  // open: out
  Driver driver_93 (.in(and_28_out), .en(and_28_out));  // open: out
  // Probe on COUNT_out
  and and_29 (CNT_TAD, TAD, NOIND, CK1);
  and and_30 (and_30_out, TAD, NOIND, STB1);
  Monoflop monoflop_4 (.C(monoflop_3_q), .R(1'b0), .Q(monoflop_4_q));  // open: nQ
  Monoflop monoflop_5 (.C(monoflop_3_nq), .R(1'b0), .Q(monoflop_5_q));  // open: nQ
  LED led_124 (.in(CNT_TAD));
  LED led_125 (.in(and_30_out));
  or or_9 (or_9_out, INST_TFL, monoflop_4_q);
  or or_10 (or_10_out, monoflop_5_q, INST_TCF);
  assign IR2RAMA = CNT_TAD ? CNT_TAD : 1'bz;  // Driver driver_94
  assign RAMD2AC_ADD = CNT_TAD ? CNT_TAD : 1'bz;  // Driver driver_95
  assign RAM_OE = CNT_TAD ? CNT_TAD : 1'bz;  // Driver driver_96
  assign driver_97_out = CNT_TAD ? CNT_TAD : 1'bz;  // Driver driver_97
  assign driver_98_out = CNT_TAD ? CNT_TAD : 1'bz;  // Driver driver_98
  Driver driver_99 (.in(and_30_out), .en(and_30_out));  // open: out
  Driver driver_100 (.in(and_30_out), .en(and_30_out));  // open: out
  Driver driver_101 (.in(and_30_out), .en(and_30_out));  // open: out
  assign AC_CK = and_30_out ? and_30_out : 1'bz;  // Driver driver_102
  assign LINK_CK = and_30_out ? and_30_out : 1'bz;  // Driver driver_103
  RS_FF_AS rs_ff_as_3 (.S(or_9_out), .R(or_10_out), .nQ(FLAG_PRNRDY));  // open: Q
  and and_31 (CNT_TAD_I, TAD, IND, PH02);
  and and_32 (and_32_out, TAD, IND, PH03);
  and and_33 (and_33_out, TAD, IND, PH04);
  and and_34 (and_34_out, TAD, IND, PH05);
  LED led_126 (.in(CNT_TAD_I));
  assign IR2RAMA = and_32_out ? and_32_out : 1'bz;  // Driver driver_104
  LED led_127 (.in(and_32_out));
  assign RAMD2IND = and_32_out ? and_32_out : 1'bz;  // Driver driver_105
  assign RAM_OE = and_32_out ? and_32_out : 1'bz;  // Driver driver_106
  assign IND_CK = and_32_out ? and_32_out : 1'bz;  // Driver driver_107
  Driver driver_108 (.in(and_32_out), .en(and_32_out));  // open: out
  assign IND2RAMA = and_33_out ? and_33_out : 1'bz;  // Driver driver_109
  LED led_128 (.in(and_33_out));
  assign RAMD2AC_ADD = and_33_out ? and_33_out : 1'bz;  // Driver driver_110
  assign RAM_OE = and_33_out ? and_33_out : 1'bz;  // Driver driver_111
  Driver driver_112 (.in(and_33_out), .en(and_33_out));  // open: out
  Driver driver_113 (.in(and_33_out), .en(and_33_out));  // open: out
  assign IND2RAMA = and_34_out ? and_34_out : 1'bz;  // Driver driver_114
  LED led_129 (.in(and_34_out));
  assign RAMD2AC_ADD = and_34_out ? and_34_out : 1'bz;  // Driver driver_115
  assign RAM_OE = and_34_out ? and_34_out : 1'bz;  // Driver driver_116
  assign AC_CK = and_34_out ? and_34_out : 1'bz;  // Driver driver_117
  assign LINK_CK = and_34_out ? and_34_out : 1'bz;  // Driver driver_118
  assign IR2RAMA = CNT_TAD_I ? CNT_TAD_I : 1'bz;  // Driver driver_119
  assign RAMD2IND = CNT_TAD_I ? CNT_TAD_I : 1'bz;  // Driver driver_120
  assign RAM_OE = CNT_TAD_I ? CNT_TAD_I : 1'bz;  // Driver driver_121
  Driver driver_122 (.in(CNT_TAD_I), .en(CNT_TAD_I));  // open: out
  Driver driver_123 (.in(CNT_TAD_I), .en(CNT_TAD_I));  // open: out
  and and_35 (CNT_TAD_IA, TAD, AUTOIND, PH02);
  and and_36 (and_36_out, TAD, AUTOIND, PH03);
  and and_37 (and_37_out, TAD, AUTOIND, PH04);
  and and_38 (and_38_out, TAD, AUTOIND, PH05);
  and and_39 (and_39_out, TAD, AUTOIND, PH06);
  LED led_130 (.in(and_39_out));
  and and_40 (and_40_out, TAD, AUTOIND, PH07);
  LED led_131 (.in(and_40_out));
  and and_41 (and_41_out, TAD, AUTOIND, PH08);
  LED led_132 (.in(and_41_out));
  assign IR2RAMA = CNT_TAD_IA ? CNT_TAD_IA : 1'bz;  // Driver driver_124
  LED led_133 (.in(CNT_TAD_IA));
  assign RAM_OE = CNT_TAD_IA ? CNT_TAD_IA : 1'bz;  // Driver driver_125
  Driver driver_126 (.in(CNT_TAD_IA), .en(CNT_TAD_IA));  // open: out
  Driver driver_127 (.in(CNT_TAD_IA), .en(CNT_TAD_IA));  // open: out
  Driver driver_128 (.in(CNT_TAD_IA), .en(CNT_TAD_IA));  // open: out
  assign IR2RAMA = and_36_out ? and_36_out : 1'bz;  // Driver driver_129
  LED led_134 (.in(and_36_out));
  assign IND_CK = and_36_out ? and_36_out : 1'bz;  // Driver driver_130
  assign RAM_OE = and_36_out ? and_36_out : 1'bz;  // Driver driver_131
  Driver driver_132 (.in(and_36_out), .en(and_36_out));  // open: out
  Driver driver_133 (.in(and_36_out), .en(and_36_out));  // open: out
  assign INC2RAMD = and_37_out ? and_37_out : 1'bz;  // Driver driver_134
  LED led_135 (.in(and_37_out));
  assign RAM_WE = and_37_out ? and_37_out : 1'bz;  // Driver driver_135
  assign IND2INC = and_37_out ? and_37_out : 1'bz;  // Driver driver_136
  Driver driver_137 (.in(and_37_out), .en(and_37_out));  // open: out
  Driver driver_138 (.in(and_37_out), .en(and_37_out));  // open: out
  assign IR2RAMA = and_38_out ? and_38_out : 1'bz;  // Driver driver_139
  LED led_136 (.in(and_38_out));
  assign RAMD2IND = and_38_out ? and_38_out : 1'bz;  // Driver driver_140
  assign RAM_OE = and_38_out ? and_38_out : 1'bz;  // Driver driver_141
  Driver driver_142 (.in(and_38_out), .en(and_38_out));  // open: out
  Driver driver_143 (.in(and_38_out), .en(and_38_out));  // open: out
  assign IR2RAMA = and_39_out ? and_39_out : 1'bz;  // Driver driver_144
  assign RAMD2IND = and_39_out ? and_39_out : 1'bz;  // Driver driver_145
  assign RAM_OE = and_39_out ? and_39_out : 1'bz;  // Driver driver_146
  assign IND_CK = and_39_out ? and_39_out : 1'bz;  // Driver driver_147
  Driver driver_148 (.in(and_39_out), .en(and_39_out));  // open: out
  assign IND2RAMA = and_40_out ? and_40_out : 1'bz;  // Driver driver_149
  assign RAMD2AC_ADD = and_40_out ? and_40_out : 1'bz;  // Driver driver_150
  assign RAM_OE = and_40_out ? and_40_out : 1'bz;  // Driver driver_151
  Driver driver_152 (.in(and_40_out), .en(and_40_out));  // open: out
  Driver driver_153 (.in(and_40_out), .en(and_40_out));  // open: out
  assign IND2RAMA = and_41_out ? and_41_out : 1'bz;  // Driver driver_154
  assign RAMD2AC_ADD = and_41_out ? and_41_out : 1'bz;  // Driver driver_155
  assign RAM_OE = and_41_out ? and_41_out : 1'bz;  // Driver driver_156
  assign AC_CK = and_41_out ? and_41_out : 1'bz;  // Driver driver_157
  assign LINK_CK = and_41_out ? and_41_out : 1'bz;  // Driver driver_158
  and and_42 (CNT_ISZ, ISZ, NOIND, PH02);
  and and_43 (and_43_out, ISZ, NOIND, PH03);
  and and_44 (and_44_out, ISZ, NOIND, PH04);
  and and_45 (and_45_out, ISZ, NOIND, PH05);
  and and_46 (and_46_out, ISZ, NOIND, INCZERO, PH06);
  LED led_137 (.in(CNT_ISZ));
  LED led_138 (.in(and_43_out));
  LED led_139 (.in(and_44_out));
  LED led_140 (.in(and_45_out));
  LED led_141 (.in(and_46_out));
  assign IR2RAMA = CNT_ISZ ? CNT_ISZ : 1'bz;  // Driver driver_159
  assign RAM_OE = CNT_ISZ ? CNT_ISZ : 1'bz;  // Driver driver_160
  Driver driver_161 (.in(CNT_ISZ), .en(CNT_ISZ));  // open: out
  Driver driver_162 (.in(CNT_ISZ), .en(CNT_ISZ));  // open: out
  Driver driver_163 (.in(CNT_ISZ), .en(CNT_ISZ));  // open: out
  assign IR2RAMA = and_43_out ? and_43_out : 1'bz;  // Driver driver_164
  assign RAM_OE = and_43_out ? and_43_out : 1'bz;  // Driver driver_165
  assign DATA_CK = and_43_out ? and_43_out : 1'bz;  // Driver driver_166
  assign LD2INC = and_43_out ? and_43_out : 1'bz;  // Driver driver_167
  Driver driver_168 (.in(and_43_out), .en(and_43_out));  // open: out
  assign IR2RAMA = and_44_out ? and_44_out : 1'bz;  // Driver driver_169
  assign RAM_WE = and_44_out ? and_44_out : 1'bz;  // Driver driver_170
  assign INC2RAMD = and_44_out ? and_44_out : 1'bz;  // Driver driver_171
  assign LD2INC = and_44_out ? and_44_out : 1'bz;  // Driver driver_172
  Driver driver_173 (.in(and_44_out), .en(and_44_out));  // open: out
  assign IR2RAMA = and_45_out ? and_45_out : 1'bz;  // Driver driver_174
  assign RAM_OE = and_45_out ? and_45_out : 1'bz;  // Driver driver_175
  assign LD2INC = and_45_out ? and_45_out : 1'bz;  // Driver driver_176
  Driver driver_177 (.in(and_45_out), .en(and_45_out));  // open: out
  Driver driver_178 (.in(and_45_out), .en(and_45_out));  // open: out
  assign PC_CK = and_46_out ? and_46_out : 1'bz;  // Driver driver_179
  assign LD2INC = and_46_out ? and_46_out : 1'bz;  // Driver driver_180
  Driver driver_181 (.in(and_46_out), .en(and_46_out));  // open: out
  Driver driver_182 (.in(and_46_out), .en(and_46_out));  // open: out
  Driver driver_183 (.in(and_46_out), .en(and_46_out));  // open: out
  and and_47 (CNT_ISZ_I, ISZ, IND, PH02);
  LED led_142 (.in(CNT_ISZ_I));
  and and_48 (and_48_out, ISZ, IND, PH03);
  LED led_143 (.in(and_48_out));
  and and_49 (and_49_out, ISZ, IND, PH04);
  LED led_144 (.in(and_49_out));
  and and_50 (and_50_out, ISZ, IND, PH05);
  LED led_145 (.in(and_50_out));
  and and_51 (and_51_out, ISZ, IND, PH06);
  LED led_146 (.in(and_51_out));
  and and_52 (and_52_out, ISZ, IND, PH07);
  LED led_147 (.in(and_52_out));
  and and_53 (and_53_out, ISZ, IND, INCZERO, PH08);
  LED led_148 (.in(and_53_out));
  assign IR2RAMA = CNT_ISZ_I ? CNT_ISZ_I : 1'bz;  // Driver driver_184
  assign RAMD2IND = CNT_ISZ_I ? CNT_ISZ_I : 1'bz;  // Driver driver_185
  assign RAM_OE = CNT_ISZ_I ? CNT_ISZ_I : 1'bz;  // Driver driver_186
  Driver driver_187 (.in(CNT_ISZ_I), .en(CNT_ISZ_I));  // open: out
  Driver driver_188 (.in(CNT_ISZ_I), .en(CNT_ISZ_I));  // open: out
  assign IR2RAMA = and_48_out ? and_48_out : 1'bz;  // Driver driver_189
  assign RAMD2IND = and_48_out ? and_48_out : 1'bz;  // Driver driver_190
  assign RAM_OE = and_48_out ? and_48_out : 1'bz;  // Driver driver_191
  assign IND_CK = and_48_out ? and_48_out : 1'bz;  // Driver driver_192
  Driver driver_193 (.in(and_48_out), .en(and_48_out));  // open: out
  assign IND2RAMA = and_49_out ? and_49_out : 1'bz;  // Driver driver_194
  assign RAM_OE = and_49_out ? and_49_out : 1'bz;  // Driver driver_195
  Driver driver_196 (.in(and_49_out), .en(and_49_out));  // open: out
  Driver driver_197 (.in(and_49_out), .en(and_49_out));  // open: out
  Driver driver_198 (.in(and_49_out), .en(and_49_out));  // open: out
  assign IND2RAMA = and_50_out ? and_50_out : 1'bz;  // Driver driver_199
  assign RAM_OE = and_50_out ? and_50_out : 1'bz;  // Driver driver_200
  assign DATA_CK = and_50_out ? and_50_out : 1'bz;  // Driver driver_201
  assign LD2INC = and_50_out ? and_50_out : 1'bz;  // Driver driver_202
  Driver driver_203 (.in(and_50_out), .en(and_50_out));  // open: out
  assign IND2RAMA = and_51_out ? and_51_out : 1'bz;  // Driver driver_204
  assign RAM_WE = and_51_out ? and_51_out : 1'bz;  // Driver driver_205
  assign INC2RAMD = and_51_out ? and_51_out : 1'bz;  // Driver driver_206
  assign LD2INC = and_51_out ? and_51_out : 1'bz;  // Driver driver_207
  Driver driver_208 (.in(and_51_out), .en(and_51_out));  // open: out
  assign IND2RAMA = and_52_out ? and_52_out : 1'bz;  // Driver driver_209
  assign RAM_OE = and_52_out ? and_52_out : 1'bz;  // Driver driver_210
  assign LD2INC = and_52_out ? and_52_out : 1'bz;  // Driver driver_211
  Driver driver_212 (.in(and_52_out), .en(and_52_out));  // open: out
  Driver driver_213 (.in(and_52_out), .en(and_52_out));  // open: out
  assign PC_CK = and_53_out ? and_53_out : 1'bz;  // Driver driver_214
  assign LD2INC = and_53_out ? and_53_out : 1'bz;  // Driver driver_215
  Driver driver_216 (.in(and_53_out), .en(and_53_out));  // open: out
  Driver driver_217 (.in(and_53_out), .en(and_53_out));  // open: out
  Driver driver_218 (.in(and_53_out), .en(and_53_out));  // open: out
  and and_54 (CNT_ISZ_IA, ISZ, AUTOIND, PH02);
  and and_55 (and_55_out, ISZ, AUTOIND, PH03);
  and and_56 (and_56_out, ISZ, AUTOIND, PH04);
  and and_57 (and_57_out, ISZ, AUTOIND, PH05);
  and and_58 (and_58_out, ISZ, AUTOIND, PH06);
  and and_59 (and_59_out, ISZ, AUTOIND, PH07);
  and and_60 (and_60_out, ISZ, AUTOIND, PH08);
  and and_61 (and_61_out, ISZ, AUTOIND, PH09);
  and and_62 (and_62_out, ISZ, AUTOIND, PH10);
  and and_63 (and_63_out, ISZ, AUTOIND, INCZERO, PH11);
  LED led_149 (.in(CNT_ISZ_IA));
  LED led_150 (.in(and_55_out));
  LED led_151 (.in(and_56_out));
  LED led_152 (.in(and_57_out));
  LED led_153 (.in(and_58_out));
  LED led_154 (.in(and_59_out));
  LED led_155 (.in(and_60_out));
  assign IND2RAMA = and_61_out ? and_61_out : 1'bz;  // Driver driver_219
  LED led_156 (.in(and_61_out));
  assign RAM_WE = and_61_out ? and_61_out : 1'bz;  // Driver driver_220
  assign INC2RAMD = and_61_out ? and_61_out : 1'bz;  // Driver driver_221
  assign LD2INC = and_61_out ? and_61_out : 1'bz;  // Driver driver_222
  Driver driver_223 (.in(and_61_out), .en(and_61_out));  // open: out
  assign IND2RAMA = and_62_out ? and_62_out : 1'bz;  // Driver driver_224
  LED led_157 (.in(and_62_out));
  assign RAM_OE = and_62_out ? and_62_out : 1'bz;  // Driver driver_225
  assign LD2INC = and_62_out ? and_62_out : 1'bz;  // Driver driver_226
  Driver driver_227 (.in(and_62_out), .en(and_62_out));  // open: out
  Driver driver_228 (.in(and_62_out), .en(and_62_out));  // open: out
  assign PC_CK = and_63_out ? and_63_out : 1'bz;  // Driver driver_229
  LED led_158 (.in(and_63_out));
  assign LD2INC = and_63_out ? and_63_out : 1'bz;  // Driver driver_230
  Driver driver_231 (.in(and_63_out), .en(and_63_out));  // open: out
  Driver driver_232 (.in(and_63_out), .en(and_63_out));  // open: out
  Driver driver_233 (.in(and_63_out), .en(and_63_out));  // open: out
  assign IR2RAMA = CNT_ISZ_IA ? CNT_ISZ_IA : 1'bz;  // Driver driver_234
  assign RAM_OE = CNT_ISZ_IA ? CNT_ISZ_IA : 1'bz;  // Driver driver_235
  Driver driver_236 (.in(CNT_ISZ_IA), .en(CNT_ISZ_IA));  // open: out
  Driver driver_237 (.in(CNT_ISZ_IA), .en(CNT_ISZ_IA));  // open: out
  Driver driver_238 (.in(CNT_ISZ_IA), .en(CNT_ISZ_IA));  // open: out
  assign IR2RAMA = and_55_out ? and_55_out : 1'bz;  // Driver driver_239
  assign IND_CK = and_55_out ? and_55_out : 1'bz;  // Driver driver_240
  assign RAM_OE = and_55_out ? and_55_out : 1'bz;  // Driver driver_241
  Driver driver_242 (.in(and_55_out), .en(and_55_out));  // open: out
  Driver driver_243 (.in(and_55_out), .en(and_55_out));  // open: out
  assign INC2RAMD = and_56_out ? and_56_out : 1'bz;  // Driver driver_244
  assign RAM_WE = and_56_out ? and_56_out : 1'bz;  // Driver driver_245
  assign IND2INC = and_56_out ? and_56_out : 1'bz;  // Driver driver_246
  Driver driver_247 (.in(and_56_out), .en(and_56_out));  // open: out
  Driver driver_248 (.in(and_56_out), .en(and_56_out));  // open: out
  assign IR2RAMA = and_57_out ? and_57_out : 1'bz;  // Driver driver_249
  assign RAMD2IND = and_57_out ? and_57_out : 1'bz;  // Driver driver_250
  assign RAM_OE = and_57_out ? and_57_out : 1'bz;  // Driver driver_251
  Driver driver_252 (.in(and_57_out), .en(and_57_out));  // open: out
  Driver driver_253 (.in(and_57_out), .en(and_57_out));  // open: out
  assign IR2RAMA = and_58_out ? and_58_out : 1'bz;  // Driver driver_254
  assign RAMD2IND = and_58_out ? and_58_out : 1'bz;  // Driver driver_255
  assign RAM_OE = and_58_out ? and_58_out : 1'bz;  // Driver driver_256
  assign IND_CK = and_58_out ? and_58_out : 1'bz;  // Driver driver_257
  Driver driver_258 (.in(and_58_out), .en(and_58_out));  // open: out
  assign IND2RAMA = and_59_out ? and_59_out : 1'bz;  // Driver driver_259
  assign RAM_OE = and_59_out ? and_59_out : 1'bz;  // Driver driver_260
  Driver driver_261 (.in(and_59_out), .en(and_59_out));  // open: out
  Driver driver_262 (.in(and_59_out), .en(and_59_out));  // open: out
  Driver driver_263 (.in(and_59_out), .en(and_59_out));  // open: out
  assign IND2RAMA = and_60_out ? and_60_out : 1'bz;  // Driver driver_264
  assign RAM_OE = and_60_out ? and_60_out : 1'bz;  // Driver driver_265
  assign DATA_CK = and_60_out ? and_60_out : 1'bz;  // Driver driver_266
  assign LD2INC = and_60_out ? and_60_out : 1'bz;  // Driver driver_267
  Driver driver_268 (.in(and_60_out), .en(and_60_out));  // open: out
  and and_64 (CNT_DCA, DCA, NOIND, CK2);
  LED led_159 (.in(CNT_DCA));
  and and_65 (and_65_out, DCA, NOIND, STB2);
  LED led_160 (.in(and_65_out));
  and and_66 (and_66_out, DCA, NOIND, CK3);
  LED led_161 (.in(and_66_out));
  assign IR2RAMA = CNT_DCA ? CNT_DCA : 1'bz;  // Driver driver_269
  assign AC2RAMD = CNT_DCA ? CNT_DCA : 1'bz;  // Driver driver_270
  Driver driver_271 (.in(CNT_DCA), .en(CNT_DCA));  // open: out
  Driver driver_272 (.in(CNT_DCA), .en(CNT_DCA));  // open: out
  Driver driver_273 (.in(CNT_DCA), .en(CNT_DCA));  // open: out
  Driver driver_274 (.in(and_65_out), .en(and_65_out));  // open: out
  Driver driver_275 (.in(and_65_out), .en(and_65_out));  // open: out
  assign RAM_WE = and_65_out ? and_65_out : 1'bz;  // Driver driver_276
  assign CLA = and_65_out ? and_65_out : 1'bz;  // Driver driver_277
  Driver driver_278 (.in(and_65_out), .en(and_65_out));  // open: out
  assign CLAx = and_66_out ? and_66_out : 1'bz;  // Driver driver_279
  assign ROT2AC = and_66_out ? and_66_out : 1'bz;  // Driver driver_280
  assign AC_CK = and_66_out ? and_66_out : 1'bz;  // Driver driver_281
  Driver driver_282 (.in(and_66_out), .en(and_66_out));  // open: out
  Driver driver_283 (.in(and_66_out), .en(and_66_out));  // open: out
  and and_67 (CNT_DCA_I, DCA, IND, PH02);
  and and_68 (and_68_out, DCA, IND, PH03);
  and and_69 (and_69_out, DCA, IND, PH04);
  and and_70 (and_70_out, DCA, IND, PH05);
  and and_71 (and_71_out, DCA, IND, PH06);
  LED led_162 (.in(CNT_DCA_I));
  LED led_163 (.in(and_68_out));
  LED led_164 (.in(and_69_out));
  LED led_165 (.in(and_70_out));
  LED led_166 (.in(and_71_out));
  assign IR2RAMA = CNT_DCA_I ? CNT_DCA_I : 1'bz;  // Driver driver_284
  assign RAMD2IND = CNT_DCA_I ? CNT_DCA_I : 1'bz;  // Driver driver_285
  assign RAM_OE = CNT_DCA_I ? CNT_DCA_I : 1'bz;  // Driver driver_286
  assign driver_287_out = CNT_DCA_I ? CNT_DCA_I : 1'bz;  // Driver driver_287
  assign driver_288_out = CNT_DCA_I ? CNT_DCA_I : 1'bz;  // Driver driver_288
  assign IR2RAMA = and_68_out ? and_68_out : 1'bz;  // Driver driver_289
  assign RAMD2IND = and_68_out ? and_68_out : 1'bz;  // Driver driver_290
  assign RAM_OE = and_68_out ? and_68_out : 1'bz;  // Driver driver_291
  assign IND_CK = and_68_out ? and_68_out : 1'bz;  // Driver driver_292
  assign driver_293_out = and_68_out ? and_68_out : 1'bz;  // Driver driver_293
  assign IND2RAMA = and_69_out ? and_69_out : 1'bz;  // Driver driver_294
  assign AC2RAMD = and_69_out ? and_69_out : 1'bz;  // Driver driver_295
  Driver driver_296 (.in(and_69_out), .en(and_69_out));  // open: out
  Driver driver_297 (.in(and_69_out), .en(and_69_out));  // open: out
  Driver driver_298 (.in(and_69_out), .en(and_69_out));  // open: out
  assign IND2RAMA = and_70_out ? and_70_out : 1'bz;  // Driver driver_299
  assign AC2RAMD = and_70_out ? and_70_out : 1'bz;  // Driver driver_300
  assign RAM_WE = and_70_out ? and_70_out : 1'bz;  // Driver driver_301
  assign CLA = and_70_out ? and_70_out : 1'bz;  // Driver driver_302
  Driver driver_303 (.in(and_70_out), .en(and_70_out));  // open: out
  assign CLAx = and_71_out ? and_71_out : 1'bz;  // Driver driver_304
  assign ROT2AC = and_71_out ? and_71_out : 1'bz;  // Driver driver_305
  assign AC_CK = and_71_out ? and_71_out : 1'bz;  // Driver driver_306
  Driver driver_307 (.in(and_71_out), .en(and_71_out));  // open: out
  Driver driver_308 (.in(and_71_out), .en(and_71_out));  // open: out
  and and_72 (CNT_DCA_IA, DCA, AUTOIND, PH02);
  and and_73 (and_73_out, DCA, AUTOIND, PH03);
  and and_74 (and_74_out, DCA, AUTOIND, PH04);
  and and_75 (and_75_out, DCA, AUTOIND, PH05);
  and and_76 (and_76_out, DCA, AUTOIND, PH06);
  assign IR2RAMA = CNT_DCA_IA ? CNT_DCA_IA : 1'bz;  // Driver driver_309
  LED led_167 (.in(CNT_DCA_IA));
  assign RAM_OE = CNT_DCA_IA ? CNT_DCA_IA : 1'bz;  // Driver driver_310
  assign driver_311_out = CNT_DCA_IA ? CNT_DCA_IA : 1'bz;  // Driver driver_311
  assign driver_312_out = CNT_DCA_IA ? CNT_DCA_IA : 1'bz;  // Driver driver_312
  assign driver_313_out = CNT_DCA_IA ? CNT_DCA_IA : 1'bz;  // Driver driver_313
  assign IR2RAMA = and_73_out ? and_73_out : 1'bz;  // Driver driver_314
  LED led_168 (.in(and_73_out));
  assign IND_CK = and_73_out ? and_73_out : 1'bz;  // Driver driver_315
  assign RAM_OE = and_73_out ? and_73_out : 1'bz;  // Driver driver_316
  assign driver_317_out = and_73_out ? and_73_out : 1'bz;  // Driver driver_317
  assign driver_318_out = and_73_out ? and_73_out : 1'bz;  // Driver driver_318
  assign INC2RAMD = and_74_out ? and_74_out : 1'bz;  // Driver driver_319
  LED led_169 (.in(and_74_out));
  assign RAM_WE = and_74_out ? and_74_out : 1'bz;  // Driver driver_320
  assign IND2INC = and_74_out ? and_74_out : 1'bz;  // Driver driver_321
  assign driver_322_out = and_74_out ? and_74_out : 1'bz;  // Driver driver_322
  assign driver_323_out = and_74_out ? and_74_out : 1'bz;  // Driver driver_323
  assign IR2RAMA = and_75_out ? and_75_out : 1'bz;  // Driver driver_324
  LED led_170 (.in(and_75_out));
  assign RAMD2IND = and_75_out ? and_75_out : 1'bz;  // Driver driver_325
  assign RAM_OE = and_75_out ? and_75_out : 1'bz;  // Driver driver_326
  assign driver_327_out = and_75_out ? and_75_out : 1'bz;  // Driver driver_327
  assign driver_328_out = and_75_out ? and_75_out : 1'bz;  // Driver driver_328
  assign IR2RAMA = and_76_out ? and_76_out : 1'bz;  // Driver driver_329
  LED led_171 (.in(and_76_out));
  assign RAMD2IND = and_76_out ? and_76_out : 1'bz;  // Driver driver_330
  assign RAM_OE = and_76_out ? and_76_out : 1'bz;  // Driver driver_331
  assign IND_CK = and_76_out ? and_76_out : 1'bz;  // Driver driver_332
  assign driver_333_out = and_76_out ? and_76_out : 1'bz;  // Driver driver_333
  and and_77 (CNT_JMS, JMS, NOIND, PH02);
  and and_78 (and_78_out, JMS, NOIND, PH03);
  and and_79 (and_79_out, JMS, NOIND, PH04);
  and and_80 (and_80_out, JMS, NOIND, PH05);
  and and_81 (and_81_out, JMS, NOIND, PH06);
  LED led_172 (.in(CNT_JMS));
  assign PC2RAMD = and_78_out ? and_78_out : 1'bz;  // Driver driver_334
  LED led_173 (.in(and_78_out));
  assign IR2RAMA = and_78_out ? and_78_out : 1'bz;  // Driver driver_335
  assign RAM_WE = and_78_out ? and_78_out : 1'bz;  // Driver driver_336
  assign IR2PC = and_78_out ? and_78_out : 1'bz;  // Driver driver_337
  assign driver_338_out = and_78_out ? and_78_out : 1'bz;  // Driver driver_338
  LED led_174 (.in(and_79_out));
  LED led_175 (.in(and_80_out));
  LED led_176 (.in(and_81_out));
  assign PC2RAMD = CNT_JMS ? CNT_JMS : 1'bz;  // Driver driver_339
  assign IR2RAMA = CNT_JMS ? CNT_JMS : 1'bz;  // Driver driver_340
  assign driver_341_out = CNT_JMS ? CNT_JMS : 1'bz;  // Driver driver_341
  assign driver_342_out = CNT_JMS ? CNT_JMS : 1'bz;  // Driver driver_342
  assign driver_343_out = CNT_JMS ? CNT_JMS : 1'bz;  // Driver driver_343
  assign IR2PC = and_79_out ? and_79_out : 1'bz;  // Driver driver_344
  assign PC_LD = and_79_out ? and_79_out : 1'bz;  // Driver driver_345
  assign PC_CK = and_79_out ? and_79_out : 1'bz;  // Driver driver_346
  assign driver_347_out = and_79_out ? and_79_out : 1'bz;  // Driver driver_347
  assign driver_348_out = and_79_out ? and_79_out : 1'bz;  // Driver driver_348
  assign driver_349_out = and_80_out ? and_80_out : 1'bz;  // Driver driver_349
  assign driver_350_out = and_80_out ? and_80_out : 1'bz;  // Driver driver_350
  assign driver_351_out = and_80_out ? and_80_out : 1'bz;  // Driver driver_351
  assign driver_352_out = and_80_out ? and_80_out : 1'bz;  // Driver driver_352
  assign driver_353_out = and_80_out ? and_80_out : 1'bz;  // Driver driver_353
  assign PC_CK = and_81_out ? and_81_out : 1'bz;  // Driver driver_354
  assign driver_355_out = and_81_out ? and_81_out : 1'bz;  // Driver driver_355
  assign driver_356_out = and_81_out ? and_81_out : 1'bz;  // Driver driver_356
  assign driver_357_out = and_81_out ? and_81_out : 1'bz;  // Driver driver_357
  Driver driver_358 (.in(and_81_out), .en(and_81_out));  // open: out
  and and_82 (CNT_JMS_I, JMS, IND, PH02);
  and and_83 (and_83_out, JMS, IND, PH03);
  and and_84 (and_84_out, JMS, IND, PH04);
  and and_85 (and_85_out, JMS, IND, PH05);
  and and_86 (and_86_out, JMS, IND, PH06);
  and and_87 (and_87_out, JMS, IND, PH07);
  and and_88 (and_88_out, JMS, IND, PH08);
  LED led_177 (.in(CNT_JMS_I));
  LED led_178 (.in(and_83_out));
  LED led_179 (.in(and_84_out));
  LED led_180 (.in(and_85_out));
  LED led_181 (.in(and_86_out));
  LED led_182 (.in(and_87_out));
  LED led_183 (.in(and_88_out));
  assign IR2RAMA = CNT_JMS_I ? CNT_JMS_I : 1'bz;  // Driver driver_359
  assign RAMD2IND = CNT_JMS_I ? CNT_JMS_I : 1'bz;  // Driver driver_360
  assign RAM_OE = CNT_JMS_I ? CNT_JMS_I : 1'bz;  // Driver driver_361
  assign driver_362_out = CNT_JMS_I ? CNT_JMS_I : 1'bz;  // Driver driver_362
  assign driver_363_out = CNT_JMS_I ? CNT_JMS_I : 1'bz;  // Driver driver_363
  assign IR2RAMA = and_83_out ? and_83_out : 1'bz;  // Driver driver_364
  assign RAMD2IND = and_83_out ? and_83_out : 1'bz;  // Driver driver_365
  assign RAM_OE = and_83_out ? and_83_out : 1'bz;  // Driver driver_366
  assign IND_CK = and_83_out ? and_83_out : 1'bz;  // Driver driver_367
  assign driver_368_out = and_83_out ? and_83_out : 1'bz;  // Driver driver_368
  assign IND2RAMA = and_84_out ? and_84_out : 1'bz;  // Driver driver_369
  assign PC2RAMD = and_84_out ? and_84_out : 1'bz;  // Driver driver_370
  Driver driver_371 (.in(and_84_out), .en(and_84_out));  // open: out
  assign driver_372_out = and_84_out ? and_84_out : 1'bz;  // Driver driver_372
  assign driver_373_out = and_84_out ? and_84_out : 1'bz;  // Driver driver_373
  assign IND2RAMA = and_85_out ? and_85_out : 1'bz;  // Driver driver_374
  assign PC2RAMD = and_85_out ? and_85_out : 1'bz;  // Driver driver_375
  assign RAM_WE = and_85_out ? and_85_out : 1'bz;  // Driver driver_376
  assign PC_LD = and_85_out ? and_85_out : 1'bz;  // Driver driver_377
  assign IND2PC = and_85_out ? and_85_out : 1'bz;  // Driver driver_378
  assign IND2PC = and_86_out ? and_86_out : 1'bz;  // Driver driver_379
  assign PC_LD = and_86_out ? and_86_out : 1'bz;  // Driver driver_380
  assign PC_CK = and_86_out ? and_86_out : 1'bz;  // Driver driver_381
  Driver driver_382 (.in(and_86_out), .en(and_86_out));  // open: out
  assign driver_383_out = and_86_out ? and_86_out : 1'bz;  // Driver driver_383
  Driver driver_384 (.in(and_87_out), .en(and_87_out));  // open: out
  Driver driver_385 (.in(and_87_out), .en(and_87_out));  // open: out
  assign driver_386_out = and_87_out ? and_87_out : 1'bz;  // Driver driver_386
  assign driver_387_out = and_87_out ? and_87_out : 1'bz;  // Driver driver_387
  assign driver_388_out = and_87_out ? and_87_out : 1'bz;  // Driver driver_388
  assign PC_CK = and_88_out ? and_88_out : 1'bz;  // Driver driver_389
  assign driver_390_out = and_88_out ? and_88_out : 1'bz;  // Driver driver_390
  assign driver_391_out = and_88_out ? and_88_out : 1'bz;  // Driver driver_391
  assign driver_392_out = and_88_out ? and_88_out : 1'bz;  // Driver driver_392
  Driver driver_393 (.in(and_88_out), .en(and_88_out));  // open: out
  and and_89 (CNT_JMS_IA, JMS, AUTOIND, PH02);
  and and_90 (and_90_out, JMS, AUTOIND, PH03);
  and and_91 (and_91_out, JMS, AUTOIND, PH04);
  and and_92 (and_92_out, JMS, AUTOIND, PH05);
  and and_93 (and_93_out, JMS, AUTOIND, PH06);
  and and_94 (and_94_out, JMS, AUTOIND, PH07);
  and and_95 (and_95_out, JMS, AUTOIND, PH08);
  and and_96 (and_96_out, JMS, AUTOIND, PH09);
  and and_97 (and_97_out, JMS, AUTOIND, PH10);
  and and_98 (and_98_out, JMS, AUTOIND, PH11);
  LED led_184 (.in(CNT_JMS_IA));
  LED led_185 (.in(and_90_out));
  LED led_186 (.in(and_91_out));
  LED led_187 (.in(and_92_out));
  LED led_188 (.in(and_93_out));
  LED led_189 (.in(and_94_out));
  LED led_190 (.in(and_95_out));
  LED led_191 (.in(and_96_out));
  LED led_192 (.in(and_97_out));
  LED led_193 (.in(and_98_out));
  assign IR2RAMA = CNT_JMS_IA ? CNT_JMS_IA : 1'bz;  // Driver driver_394
  assign RAM_OE = CNT_JMS_IA ? CNT_JMS_IA : 1'bz;  // Driver driver_395
  assign driver_396_out = CNT_JMS_IA ? CNT_JMS_IA : 1'bz;  // Driver driver_396
  assign driver_397_out = CNT_JMS_IA ? CNT_JMS_IA : 1'bz;  // Driver driver_397
  assign driver_398_out = CNT_JMS_IA ? CNT_JMS_IA : 1'bz;  // Driver driver_398
  assign IR2RAMA = and_90_out ? and_90_out : 1'bz;  // Driver driver_399
  assign IND_CK = and_90_out ? and_90_out : 1'bz;  // Driver driver_400
  assign RAM_OE = and_90_out ? and_90_out : 1'bz;  // Driver driver_401
  assign driver_402_out = and_90_out ? and_90_out : 1'bz;  // Driver driver_402
  assign driver_403_out = and_90_out ? and_90_out : 1'bz;  // Driver driver_403
  assign INC2RAMD = and_91_out ? and_91_out : 1'bz;  // Driver driver_404
  assign RAM_WE = and_91_out ? and_91_out : 1'bz;  // Driver driver_405
  assign IND2INC = and_91_out ? and_91_out : 1'bz;  // Driver driver_406
  Driver driver_407 (.in(and_91_out), .en(and_91_out));  // open: out
  assign driver_408_out = and_91_out ? and_91_out : 1'bz;  // Driver driver_408
  assign IR2RAMA = and_92_out ? and_92_out : 1'bz;  // Driver driver_409
  assign RAMD2IND = and_92_out ? and_92_out : 1'bz;  // Driver driver_410
  assign RAM_OE = and_92_out ? and_92_out : 1'bz;  // Driver driver_411
  assign driver_412_out = and_92_out ? and_92_out : 1'bz;  // Driver driver_412
  assign driver_413_out = and_92_out ? and_92_out : 1'bz;  // Driver driver_413
  assign IR2RAMA = and_93_out ? and_93_out : 1'bz;  // Driver driver_414
  assign RAMD2IND = and_93_out ? and_93_out : 1'bz;  // Driver driver_415
  assign RAM_OE = and_93_out ? and_93_out : 1'bz;  // Driver driver_416
  assign IND_CK = and_93_out ? and_93_out : 1'bz;  // Driver driver_417
  assign driver_418_out = and_93_out ? and_93_out : 1'bz;  // Driver driver_418
  assign IND2RAMA = and_94_out ? and_94_out : 1'bz;  // Driver driver_419
  assign PC2RAMD = and_94_out ? and_94_out : 1'bz;  // Driver driver_420
  Driver driver_421 (.in(and_94_out), .en(and_94_out));  // open: out
  assign driver_422_out = and_94_out ? and_94_out : 1'bz;  // Driver driver_422
  assign driver_423_out = and_94_out ? and_94_out : 1'bz;  // Driver driver_423
  assign IND2RAMA = and_95_out ? and_95_out : 1'bz;  // Driver driver_424
  assign PC2RAMD = and_95_out ? and_95_out : 1'bz;  // Driver driver_425
  assign RAM_WE = and_95_out ? and_95_out : 1'bz;  // Driver driver_426
  assign PC_LD = and_95_out ? and_95_out : 1'bz;  // Driver driver_427
  assign IND2PC = and_95_out ? and_95_out : 1'bz;  // Driver driver_428
  assign IND2PC = and_96_out ? and_96_out : 1'bz;  // Driver driver_429
  assign PC_LD = and_96_out ? and_96_out : 1'bz;  // Driver driver_430
  assign PC_CK = and_96_out ? and_96_out : 1'bz;  // Driver driver_431
  Driver driver_432 (.in(and_96_out), .en(and_96_out));  // open: out
  assign driver_433_out = and_96_out ? and_96_out : 1'bz;  // Driver driver_433
  Driver driver_434 (.in(and_97_out), .en(and_97_out));  // open: out
  Driver driver_435 (.in(and_97_out), .en(and_97_out));  // open: out
  assign driver_436_out = and_97_out ? and_97_out : 1'bz;  // Driver driver_436
  assign driver_437_out = and_97_out ? and_97_out : 1'bz;  // Driver driver_437
  assign driver_438_out = and_97_out ? and_97_out : 1'bz;  // Driver driver_438
  assign PC_CK = and_98_out ? and_98_out : 1'bz;  // Driver driver_439
  assign driver_440_out = and_98_out ? and_98_out : 1'bz;  // Driver driver_440
  assign driver_441_out = and_98_out ? and_98_out : 1'bz;  // Driver driver_441
  assign driver_442_out = and_98_out ? and_98_out : 1'bz;  // Driver driver_442
  Driver driver_443 (.in(and_98_out), .en(and_98_out));  // open: out
  and and_99 (CNT_JMP, JMP, NOIND, CK1);
  and and_100 (and_100_out, JMP, NOIND, STB1);
  LED led_194 (.in(CNT_JMP));
  LED led_195 (.in(and_100_out));
  assign IR2PC = CNT_JMP ? CNT_JMP : 1'bz;  // Driver driver_444
  assign PC_LD = CNT_JMP ? CNT_JMP : 1'bz;  // Driver driver_445
  assign driver_446_out = CNT_JMP ? CNT_JMP : 1'bz;  // Driver driver_446
  assign driver_447_out = CNT_JMP ? CNT_JMP : 1'bz;  // Driver driver_447
  assign driver_448_out = CNT_JMP ? CNT_JMP : 1'bz;  // Driver driver_448
  Driver driver_449 (.in(and_100_out), .en(and_100_out));  // open: out
  Driver driver_450 (.in(and_100_out), .en(and_100_out));  // open: out
  assign PC_CK = and_100_out ? and_100_out : 1'bz;  // Driver driver_451
  assign driver_452_out = and_100_out ? and_100_out : 1'bz;  // Driver driver_452
  assign driver_453_out = and_100_out ? and_100_out : 1'bz;  // Driver driver_453
  and and_101 (CNT_JMP_I, JMP, IND, PH02);
  and and_102 (and_102_out, JMP, IND, PH03);
  LED led_196 (.in(CNT_JMP_I));
  LED led_197 (.in(and_102_out));
  assign IR2RAMA = CNT_JMP_I ? CNT_JMP_I : 1'bz;  // Driver driver_454
  assign RAMD2PC = CNT_JMP_I ? CNT_JMP_I : 1'bz;  // Driver driver_455
  assign RAM_OE = CNT_JMP_I ? CNT_JMP_I : 1'bz;  // Driver driver_456
  assign driver_457_out = CNT_JMP_I ? CNT_JMP_I : 1'bz;  // Driver driver_457
  assign driver_458_out = CNT_JMP_I ? CNT_JMP_I : 1'bz;  // Driver driver_458
  assign IR2RAMA = and_102_out ? and_102_out : 1'bz;  // Driver driver_459
  assign RAMD2PC = and_102_out ? and_102_out : 1'bz;  // Driver driver_460
  assign RAM_OE = and_102_out ? and_102_out : 1'bz;  // Driver driver_461
  assign PC_LD = and_102_out ? and_102_out : 1'bz;  // Driver driver_462
  assign PC_CK = and_102_out ? and_102_out : 1'bz;  // Driver driver_463
  and and_103 (CNT_JMP_IA, JMP, AUTOIND, PH02);
  and and_104 (and_104_out, JMP, AUTOIND, PH03);
  and and_105 (and_105_out, JMP, AUTOIND, PH04);
  and and_106 (and_106_out, JMP, AUTOIND, PH05);
  and and_107 (and_107_out, JMP, AUTOIND, PH06);
  LED led_198 (.in(CNT_JMP_IA));
  LED led_199 (.in(and_104_out));
  LED led_200 (.in(and_105_out));
  LED led_201 (.in(and_106_out));
  LED led_202 (.in(and_107_out));
  assign IR2RAMA = CNT_JMP_IA ? CNT_JMP_IA : 1'bz;  // Driver driver_464
  assign RAM_OE = CNT_JMP_IA ? CNT_JMP_IA : 1'bz;  // Driver driver_465
  assign driver_466_out = CNT_JMP_IA ? CNT_JMP_IA : 1'bz;  // Driver driver_466
  assign driver_467_out = CNT_JMP_IA ? CNT_JMP_IA : 1'bz;  // Driver driver_467
  assign driver_468_out = CNT_JMP_IA ? CNT_JMP_IA : 1'bz;  // Driver driver_468
  assign IR2RAMA = and_104_out ? and_104_out : 1'bz;  // Driver driver_469
  assign IND_CK = and_104_out ? and_104_out : 1'bz;  // Driver driver_470
  assign RAM_OE = and_104_out ? and_104_out : 1'bz;  // Driver driver_471
  assign driver_472_out = and_104_out ? and_104_out : 1'bz;  // Driver driver_472
  assign driver_473_out = and_104_out ? and_104_out : 1'bz;  // Driver driver_473
  assign INC2RAMD = and_105_out ? and_105_out : 1'bz;  // Driver driver_474
  assign RAM_WE = and_105_out ? and_105_out : 1'bz;  // Driver driver_475
  assign IND2INC = and_105_out ? and_105_out : 1'bz;  // Driver driver_476
  assign driver_477_out = and_105_out ? and_105_out : 1'bz;  // Driver driver_477
  assign driver_478_out = and_105_out ? and_105_out : 1'bz;  // Driver driver_478
  assign IR2RAMA = and_106_out ? and_106_out : 1'bz;  // Driver driver_479
  assign RAMD2PC = and_106_out ? and_106_out : 1'bz;  // Driver driver_480
  assign RAM_OE = and_106_out ? and_106_out : 1'bz;  // Driver driver_481
  assign driver_482_out = and_106_out ? and_106_out : 1'bz;  // Driver driver_482
  assign driver_483_out = and_106_out ? and_106_out : 1'bz;  // Driver driver_483
  assign IR2RAMA = and_107_out ? and_107_out : 1'bz;  // Driver driver_484
  assign RAMD2PC = and_107_out ? and_107_out : 1'bz;  // Driver driver_485
  assign RAM_OE = and_107_out ? and_107_out : 1'bz;  // Driver driver_486
  assign PC_LD = and_107_out ? and_107_out : 1'bz;  // Driver driver_487
  assign PC_CK = and_107_out ? and_107_out : 1'bz;  // Driver driver_488
  and and_108 (CNT_OPR1, OPR1, 1'b1, CK1);
  and and_109 (and_109_out, OPR1, 1'b1, STB1);
  LED led_203 (.in(CNT_OPR1));
  LED led_204 (.in(and_109_out));
  assign ROT2AC = CNT_OPR1 ? CNT_OPR1 : 1'bz;  // Driver driver_489
  Driver driver_490 (.in(CNT_OPR1), .en(CNT_OPR1));  // open: out
  Driver driver_491 (.in(CNT_OPR1), .en(CNT_OPR1));  // open: out
  Driver driver_492 (.in(CNT_OPR1), .en(CNT_OPR1));  // open: out
  Driver driver_493 (.in(CNT_OPR1), .en(CNT_OPR1));  // open: out
  assign AC_CK = and_109_out ? and_109_out : 1'bz;  // Driver driver_494
  assign LINK_CK = and_109_out ? and_109_out : 1'bz;  // Driver driver_495
  Driver driver_496 (.in(and_109_out), .en(and_109_out));  // open: out
  Driver driver_497 (.in(and_109_out), .en(and_109_out));  // open: out
  Driver driver_498 (.in(and_109_out), .en(and_109_out));  // open: out
  Driver driver_499 (.in(and_109_out), .en(and_109_out));  // open: out
  and and_110 (CNT_OPR2, OPR2, 1'b1, CK1);
  and and_111 (and_111_out, OPR2, SKIP, STB1);
  and and_112 (and_112_out, OPR2, 1'b1, CK2);
  LED led_205 (.in(and_112_out));
  and and_113 (and_113_out, OPR2, 1'b1, STB2);
  assign ROT2AC = CNT_OPR2 ? CNT_OPR2 : 1'bz;  // Driver driver_500
  LED led_206 (.in(CNT_OPR2));
  Driver driver_501 (.in(CNT_OPR2), .en(CNT_OPR2));  // open: out
  Driver driver_502 (.in(CNT_OPR2), .en(CNT_OPR2));  // open: out
  Driver driver_503 (.in(CNT_OPR2), .en(CNT_OPR2));  // open: out
  Driver driver_504 (.in(CNT_OPR2), .en(CNT_OPR2));  // open: out
  assign driver_505_out = and_111_out ? and_111_out : 1'bz;  // Driver driver_505
  LED led_207 (.in(and_111_out));
  assign PC_CK = and_111_out ? and_111_out : 1'bz;  // Driver driver_506
  Driver driver_507 (.in(and_111_out), .en(and_111_out));  // open: out
  Driver driver_508 (.in(and_111_out), .en(and_111_out));  // open: out
  Driver driver_509 (.in(and_111_out), .en(and_111_out));  // open: out
  assign ROT2AC = and_112_out ? and_112_out : 1'bz;  // Driver driver_510
  Driver driver_511 (.in(and_112_out), .en(and_112_out));  // open: out
  Driver driver_512 (.in(and_112_out), .en(and_112_out));  // open: out
  Driver driver_513 (.in(and_112_out), .en(and_112_out));  // open: out
  Driver driver_514 (.in(and_112_out), .en(and_112_out));  // open: out
  Driver driver_515 (.in(and_113_out), .en(and_113_out));  // open: out
  LED led_208 (.in(and_113_out));
  assign AC_CK = and_113_out ? and_113_out : 1'bz;  // Driver driver_516
  Driver driver_517 (.in(and_113_out), .en(and_113_out));  // open: out
  Driver driver_518 (.in(and_113_out), .en(and_113_out));  // open: out
  Driver driver_519 (.in(and_113_out), .en(and_113_out));  // open: out
  not not_4 (not_4_out, OPR_SWP);
  not not_5 (not_5_out, OPR_SWP);
  and and_114 (CNT_OPR3, OPR3, 1'b1, CK1);
  and and_115 (and_115_out, OPR3, not_4_out, STB1);
  and and_116 (and_116_out, OPR3, 1'b1, CK2);
  and and_117 (and_117_out, OPR3, not_5_out, STB2);
  LED led_209 (.in(CNT_OPR3));
  LED led_210 (.in(and_115_out));
  LED led_211 (.in(and_116_out));
  LED led_212 (.in(and_117_out));
  assign ROT2AC = CNT_OPR3 ? CNT_OPR3 : 1'bz;  // Driver driver_520
  Driver driver_521 (.in(CNT_OPR3), .en(CNT_OPR3));  // open: out
  Driver driver_522 (.in(CNT_OPR3), .en(CNT_OPR3));  // open: out
  Driver driver_523 (.in(CNT_OPR3), .en(CNT_OPR3));  // open: out
  Driver driver_524 (.in(CNT_OPR3), .en(CNT_OPR3));  // open: out
  Driver driver_525 (.in(and_115_out), .en(and_115_out));  // open: out
  Driver driver_526 (.in(and_115_out), .en(and_115_out));  // open: out
  assign MQ_CK = and_115_out ? and_115_out : 1'bz;  // Driver driver_527
  Driver driver_528 (.in(and_115_out), .en(and_115_out));  // open: out
  Driver driver_529 (.in(and_115_out), .en(and_115_out));  // open: out
  Driver driver_530 (.in(and_115_out), .en(and_115_out));  // open: out
  assign ROT2AC = and_116_out ? and_116_out : 1'bz;  // Driver driver_531
  Driver driver_532 (.in(and_116_out), .en(and_116_out));  // open: out
  Driver driver_533 (.in(and_116_out), .en(and_116_out));  // open: out
  Driver driver_534 (.in(and_116_out), .en(and_116_out));  // open: out
  Driver driver_535 (.in(and_116_out), .en(and_116_out));  // open: out
  Driver driver_536 (.in(and_117_out), .en(and_117_out));  // open: out
  assign AC_CK = and_117_out ? and_117_out : 1'bz;  // Driver driver_537
  Driver driver_538 (.in(and_117_out), .en(and_117_out));  // open: out
  Driver driver_539 (.in(and_117_out), .en(and_117_out));  // open: out
  Driver driver_540 (.in(and_117_out), .en(and_117_out));  // open: out
  Demultiplexer #(.Selector_Bits(3)) demultiplexer_1 (
    .sel(BUS_IR[2:0]), .in(IOT_DEVHSR), .out_0(demultiplexer_1_out_0), .out_1(demultiplexer_1_out_1),
    .out_2(demultiplexer_1_out_2), .out_3(demultiplexer_1_out_3), .out_4(demultiplexer_1_out_4),
    .out_5(demultiplexer_1_out_5), .out_6(demultiplexer_1_out_6), .out_7(demultiplexer_1_out_7));
  LED led_213 (.in(IOT_DEVHSR));
  and and_118 (and_118_out, OPR3, OPR_SWP, STB1);
  LED led_214 (.in(and_118_out));
  LED led_215 (.in(IOT));
  assign MQ_CK = and_118_out ? and_118_out : 1'bz;  // Driver driver_541
  assign AC_CK = and_118_out ? and_118_out : 1'bz;  // Driver driver_542
  Driver driver_543 (.in(and_118_out), .en(and_118_out));  // open: out
  Driver driver_544 (.in(and_118_out), .en(and_118_out));  // open: out
  Driver driver_545 (.in(and_118_out), .en(and_118_out));  // open: out
  or or_11 (or_11_out, PH02, PH03, PH04, PH05, PH06, PH07, PH08, PH09, PH10, PH11);
  // Probe on BUS_IR[2:0]
  // Probe on BUS_IR[8:3]
  and and_119 (and_119_out, or_11_out, IOT);
  Demultiplexer #(.Selector_Bits(3)) demultiplexer_2 (
    .sel(BUS_IR[2:0]), .in(IOT_DEVKBD), .out_0(INST_KCF), .out_1(INST_KSF), .out_2(INST_KCC),
    .out_3(demultiplexer_2_out_3), .out_4(INST_KRS), .out_5(INST_KIE), .out_6(INST_KRB),
    .out_7(demultiplexer_2_out_7));
  LED led_216 (.in(IOT_DEVKBD));
  Demultiplexer #(.Selector_Bits(3)) demultiplexer_3 (
    .sel(BUS_IR[2:0]), .in(IOT_DEVPRI), .out_0(INST_TFL), .out_1(INST_TSF), .out_2(INST_TCF),
    .out_3(demultiplexer_3_out_3), .out_4(INST_TPC), .out_5(INST_TSK), .out_6(INST_TLS),
    .out_7(demultiplexer_3_out_7));
  LED led_217 (.in(IOT_DEVPRI));
  Demultiplexer #(.Selector_Bits(6)) demultiplexer_4 (
    .sel(BUS_IR[8:3]), .in(and_119_out), .out_0(IOT_DEVCPU), .out_1(IOT_DEVHSR), .out_2(IOT_DEVHSP),
    .out_3(IOT_DEVKBD), .out_4(IOT_DEVPRI), .out_5(IOT_5), .out_6(IOT_6), .out_7(IOT_7), .out_8(IOT_8),
    .out_9(IOT_9), .out_10(demultiplexer_4_out_10), .out_11(demultiplexer_4_out_11),
    .out_12(demultiplexer_4_out_12), .out_13(demultiplexer_4_out_13), .out_14(demultiplexer_4_out_14),
    .out_15(demultiplexer_4_out_15), .out_16(demultiplexer_4_out_16), .out_17(demultiplexer_4_out_17),
    .out_18(demultiplexer_4_out_18), .out_19(demultiplexer_4_out_19), .out_20(demultiplexer_4_out_20),
    .out_21(demultiplexer_4_out_21), .out_22(demultiplexer_4_out_22), .out_23(demultiplexer_4_out_23),
    .out_24(demultiplexer_4_out_24), .out_25(demultiplexer_4_out_25), .out_26(demultiplexer_4_out_26),
    .out_27(demultiplexer_4_out_27), .out_28(demultiplexer_4_out_28), .out_29(demultiplexer_4_out_29),
    .out_30(demultiplexer_4_out_30), .out_31(demultiplexer_4_out_31), .out_32(demultiplexer_4_out_32),
    .out_33(demultiplexer_4_out_33), .out_34(demultiplexer_4_out_34), .out_35(demultiplexer_4_out_35),
    .out_36(demultiplexer_4_out_36), .out_37(demultiplexer_4_out_37), .out_38(demultiplexer_4_out_38),
    .out_39(demultiplexer_4_out_39), .out_40(demultiplexer_4_out_40), .out_41(demultiplexer_4_out_41),
    .out_42(demultiplexer_4_out_42), .out_43(demultiplexer_4_out_43), .out_44(demultiplexer_4_out_44),
    .out_45(demultiplexer_4_out_45), .out_46(demultiplexer_4_out_46), .out_47(demultiplexer_4_out_47),
    .out_48(demultiplexer_4_out_48), .out_49(demultiplexer_4_out_49), .out_50(demultiplexer_4_out_50),
    .out_51(demultiplexer_4_out_51), .out_52(demultiplexer_4_out_52), .out_53(demultiplexer_4_out_53),
    .out_54(demultiplexer_4_out_54), .out_55(demultiplexer_4_out_55), .out_56(demultiplexer_4_out_56),
    .out_57(demultiplexer_4_out_57), .out_58(demultiplexer_4_out_58), .out_59(demultiplexer_4_out_59),
    .out_60(demultiplexer_4_out_60), .out_61(demultiplexer_4_out_61), .out_62(demultiplexer_4_out_62),
    .out_63(demultiplexer_4_out_63));
  or or_12 (IOT_6x, demultiplexer_4_out_60, demultiplexer_4_out_61, demultiplexer_4_out_63, demultiplexer_4_out_62);
  or or_13 (IOT_4x, demultiplexer_4_out_40, demultiplexer_4_out_41, demultiplexer_4_out_42, demultiplexer_4_out_43, demultiplexer_4_out_44, demultiplexer_4_out_46, demultiplexer_4_out_47, demultiplexer_4_out_48, demultiplexer_4_out_49, demultiplexer_4_out_45);
  or or_14 (IOT_5x, demultiplexer_4_out_50, demultiplexer_4_out_51, demultiplexer_4_out_52, demultiplexer_4_out_53, demultiplexer_4_out_54, demultiplexer_4_out_56, demultiplexer_4_out_57, demultiplexer_4_out_58, demultiplexer_4_out_59, demultiplexer_4_out_55);
  or or_15 (IOT_2x, demultiplexer_4_out_20, demultiplexer_4_out_21, demultiplexer_4_out_22, demultiplexer_4_out_23, demultiplexer_4_out_24, demultiplexer_4_out_26, demultiplexer_4_out_27, demultiplexer_4_out_28, demultiplexer_4_out_29, demultiplexer_4_out_25);
  or or_16 (IOT_3x, demultiplexer_4_out_30, demultiplexer_4_out_31, demultiplexer_4_out_32, demultiplexer_4_out_33, demultiplexer_4_out_34, demultiplexer_4_out_36, demultiplexer_4_out_37, demultiplexer_4_out_38, demultiplexer_4_out_39, demultiplexer_4_out_35);
  or or_17 (IOT_1x, demultiplexer_4_out_10, demultiplexer_4_out_11, demultiplexer_4_out_12, demultiplexer_4_out_13, demultiplexer_4_out_14, demultiplexer_4_out_16, demultiplexer_4_out_17, demultiplexer_4_out_18, demultiplexer_4_out_19, demultiplexer_4_out_15);
  // Probe on BUS_IR
  Demultiplexer #(.Selector_Bits(3)) demultiplexer_5 (
    .sel(BUS_IR[11:9]), .in(1'b1), .out_0(AND), .out_1(TAD), .out_2(ISZ), .out_3(DCA), .out_4(JMS),
    .out_5(JMP), .out_6(IOT), .out_7(OPR));
  LED led_218 (.in(OPR));
  Demultiplexer #(.Selector_Bits(2)) demultiplexer_6 (
    .sel({BUS_IR[8], BUS_IR[0]}), .in(OPR), .out_0(demultiplexer_6_out_0), .out_1(demultiplexer_6_out_1),
    .out_2(OPR2), .out_3(OPR3));
  and and_120 (and_120_out, BUS_IR[3], ~BUS_IR[4], ~BUS_IR[5], ~BUS_IR[6], ~BUS_IR[7], BUS_IR[8]);  // And
  LED led_219 (.in(and_120_out));
  not not_6 (not_6_out, BUS_IR[8]);
  or or_18 (OPR1, demultiplexer_6_out_0, demultiplexer_6_out_1);
  nor nor_2 (nor_2_out, and_120_out, not_6_out);
  LED led_220 (.in(OPR1));
  LED led_221 (.in(nor_2_out));
  nor nor_3 (nor_3_out, OPR, IOT);
  nor nor_4 (nor_4_out, BUS_IR[0], BUS_IR[1], BUS_IR[2], BUS_IR[3], BUS_IR[4], BUS_IR[5], BUS_IR[6], BUS_IR[7]);
  and and_121 (AUTOIND, nor_3_out, and_120_out);
  and and_122 (IND, nor_3_out, nor_2_out);
  and and_123 (NOIND, nor_3_out, not_6_out);
  and and_124 (MP, nor_3_out, BUS_IR[7]);
  and and_125 (OPR_IAC, BUS_IR[0], OPR1);
  LED led_222 (.in(OPR_IAC));
  and and_126 (OPR_X2, BUS_IR[1], OPR1);
  LED led_223 (.in(OPR_X2));
  and and_127 (OPR_LEFT, BUS_IR[2], OPR1);
  LED led_224 (.in(OPR_LEFT));
  and and_128 (OPR_RIGHT, BUS_IR[3], OPR1);
  LED led_225 (.in(OPR_RIGHT));
  and and_129 (OPR_CML, BUS_IR[4], OPR1);
  LED led_226 (.in(OPR_CML));
  and and_130 (OPR_CMA, BUS_IR[5], OPR1);
  LED led_227 (.in(OPR_CMA));
  and and_131 (OPR_CLL, BUS_IR[6], OPR1);
  LED led_228 (.in(OPR_CLL));
  and and_132 (OPR_CLA1, BUS_IR[7], OPR1);
  LED led_229 (.in(OPR_CLA1));
  and and_133 (OPR_NA1, BUS_IR[0], OPR2);
  LED led_230 (.in(OPR_NA1));
  and and_134 (OPR_HLT, BUS_IR[1], OPR2);
  LED led_231 (.in(OPR_HLT));
  and and_135 (OPR_OSR, BUS_IR[2], OPR2);
  LED led_232 (.in(OPR_OSR));
  and and_136 (OPR_TSTINV, BUS_IR[3], OPR2);
  LED led_233 (.in(OPR_TSTINV));
  and and_137 (OPR_SNLSZL, BUS_IR[4], OPR2);
  LED led_234 (.in(OPR_SNLSZL));
  and and_138 (OPR_SZASNA, BUS_IR[5], OPR2);
  LED led_235 (.in(OPR_SZASNA));
  and and_139 (OPR_SMASPA, BUS_IR[6], OPR2);
  LED led_236 (.in(OPR_SMASPA));
  and and_140 (OPR_CLA2, BUS_IR[7], OPR2);
  LED led_237 (.in(OPR_CLA2));
  and and_141 (and_141_out, OPR3, BUS_IR[0]);
  and and_142 (and_142_out[0], OPR3, BUS_IR[1]);
  and and_143 (and_142_out[1], OPR3, BUS_IR[2]);
  and and_144 (and_142_out[2], OPR3, BUS_IR[3]);
  and and_145 (and_145_out, OPR3, BUS_IR[4]);
  and and_146 (OPR_SCA, OPR3, BUS_IR[5]);
  and and_147 (and_147_out, OPR3, BUS_IR[6]);
  and and_148 (OPR_CLA3, OPR3, BUS_IR[7]);
  LED led_238 (.in(AUTOIND));
  LED led_239 (.in(IND));
  LED led_240 (.in(NOIND));
  LED led_241 (.in(MP));
  LED led_242 (.in(OPR3));
  LED led_243 (.in(and_141_out));
  LED led_244 (.in(and_142_out[0]));
  LED led_245 (.in(and_142_out[1]));
  LED led_246 (.in(and_142_out[2]));
  LED led_247 (.in(and_145_out));
  LED led_248 (.in(OPR_SCA));
  LED led_249 (.in(and_147_out));
  LED led_250 (.in(OPR_CLA3));
  and and_149 (OPR_NOP, nor_4_out, OPR);
  LED led_251 (.in(OPR1));
  LED led_252 (.in(OPR2));
  nand nand_1 (nand_1_out, and_145_out, and_147_out);
  LED led_253 (.in(OPR_NOP));
  LED led_254 (.in(nand_1_out));
  Seven_Seg_Hex seven_seg_hex_40 (.d(CK_NUM), .dp(1'b0));
  and and_150 (OPR_MQL, and_145_out, and_145_out);
  not not_7 (OPR_SWP, nand_1_out);
  and and_151 (OPR_MQA, and_147_out, and_147_out);
  // Probe on LATCHED_PC
  LED led_255 (.in(PH_FIRST));
  LED led_256 (.in(OPR_MQL));
  LED led_257 (.in(OPR_MQA));
  LED led_258 (.in(PH_STB));
  LED led_259 (.in(PH_LAST));
  Decoder #(.Selector_Bits(3)) decoder_2 (
    .sel(and_142_out), .out_0(OPR_OPERATION), .out_1(OPR_SCL), .out_2(OPR_MUY), .out_3(OPR_DVI),
    .out_4(OPR_NMI), .out_5(OPR_SHL), .out_6(OPR_ASL), .out_7(OPR_LSR));
  LED led_260 (.in(OPR_OPERATION));
  LED led_261 (.in(OPR_SCL));
  LED led_262 (.in(OPR_MUY));
  LED led_263 (.in(OPR_DVI));
  LED led_264 (.in(OPR_NMI));
  LED led_265 (.in(OPR_SHL));
  LED led_266 (.in(OPR_ASL));
  LED led_267 (.in(OPR_LSR));
  PullDown pulldown_4 (.out(IR2PC));
  PullDown pulldown_5 (.out(IND2PC));
  PullDown pulldown_6 (.out(RAMD2PC));
  PullDown pulldown_7 (.out(ROT2AC));
  PullDown pulldown_8 (.out(RAMD2AC_ADD));
  PullDown pulldown_9 (.out(PC_LD));
  PullDown pulldown_10 (.out(IND2RAMA));
  PullDown pulldown_11 (.out(INC2RAMD));
  PullDown pulldown_12 (.out(PC2RAMD));
  PullDown pulldown_13 (.out(IR2RAMA));
  PullDown pulldown_14 (.out(IND2INC));
  PullDown pulldown_15 (.out(LD2INC));
  PullDown pulldown_16 (.out(RAMA_HOLD));
  PullDown pulldown_17 (.out(DATA_CK));
  PullDown pulldown_18 (.out(IR_CK));
  PullDown pulldown_19 (.out(PC_CK));
  PullDown pulldown_20 (.out(AC_CK));
  PullDown pulldown_21 (.out(IND_CK));
  PullDown pulldown_22 (.out(LINK_CK));
  PullDown pulldown_23 (.out(RAM_WE));
  PullDown pulldown_24 (.out(RAM_OE));
  PullDown pulldown_25 (.out(MQ_CK));
  and and_152 (i_iac, OPR_IAC, 1'b1);
  and and_153 (i_cll, OPR_CLL, 1'b1);
  and and_154 (i_cma, OPR_CMA, 1'b1);
  and and_155 (i_cml, OPR_CML, 1'b1);
  and and_156 (i_osr, OPR_OSR, 1'b1);
  and and_157 (i_hlt, OPR_HLT, 1'b1);
  or or_19 (i_cla, OPR_CLA1, OPR_CLA2);
  and and_158 (i_nop, OPR_NOP, 1'b1);
  and and_159 (i_ral, OPR_LEFT, ~OPR_X2);  // And
  and and_160 (i_rar, OPR_RIGHT, ~OPR_X2);  // And
  and and_161 (i_rtl, OPR_LEFT, OPR_X2);
  and and_162 (i_rtr, OPR_RIGHT, OPR_X2);
  and and_163 (i_snl, OPR_SNLSZL, ~OPR_TSTINV);  // And
  and and_164 (i_sza, OPR_SZASNA, ~OPR_TSTINV);  // And
  and and_165 (i_sma, OPR_SMASPA, ~OPR_TSTINV);  // And
  and and_166 (i_szl, OPR_SNLSZL, OPR_TSTINV);
  and and_167 (i_sna, OPR_SZASNA, OPR_TSTINV);
  and and_168 (i_spa, OPR_SMASPA, OPR_TSTINV);
  and and_169 (i_skp, ~OPR_SNLSZL, ~OPR_SZASNA, ~OPR_SMASPA, OPR_TSTINV);  // And

  // Other names for the same wires on the sheet: RAMADDR[11:0] = {RA3, RA2, RA1, RA0}; PI0[2:0] = PCIN[2:0];
  //   PI1[2:0] = PCIN[5:3]; PI2[2:0] = PCIN[8:6]; PI3[2:0] = PCIN[11:9]; AC0[2:0] = AC[2:0]; AC1[2:0] = AC[5:3];
  //   AC2[2:0] = AC[8:6]; AC3[2:0] = AC[11:9]; IR0[2:0] = BUS_IR[2:0]; IR1[2:0] = BUS_IR[5:3]; IR2[2:0] = BUS_IR[8:6];
  //   IR3[2:0] = BUS_IR[11:9]; PC0[2:0] = BUS_PC[2:0]; PC1[2:0] = BUS_PC[5:3]; PC2[2:0] = BUS_PC[8:6];
  //   PC3[2:0] = BUS_PC[11:9]; DATA[11:0] = {DA3, DA2, DA1, DA0}; INDOUT[11:0] = {IND3, IND2, IND1, IND0};
  //   MQ0[2:0] = MQ[2:0]; MQ1[2:0] = MQ[5:3]; MQ2[2:0] = MQ[8:6]; MQ3[2:0] = MQ[11:9]; RD0[2:0] = RAMDATA[2:0];
  //   RD1[2:0] = RAMDATA[5:3]; RD2[2:0] = RAMDATA[8:6]; RD3[2:0] = RAMDATA[11:9]; XTAL = clk

  // Notes on the sheet:
  //   clk: Hz: 2147483647
  //   PCIN
  //   PC
  //   IR
  //   AC
  //   MQ
  //   IND
  //   RAM-A
  //   RAM-D
  //   PC-IN
  //   DATA
  //   ACCUMULATOR
  //   PCOUT
  //   C
  //   LINK
  //   KCF
  //   NOP
  //   PDP-8/X
  //   Rev 0.1
  //   TAD
  //   KSF
  //   CLA
  //   STATE
  //   INSTRUCTION
  //   RUN
  //   HALT
  //   PC=0200
  //   BREAKPOINT
  //   MAIN DATA-PATHS
  //   RAMADDR
  //   KCC
  //   KRS
  //   CLL
  //   KIE
  //   CMA
  //   AND
  //   START/STOP/STEP
  //   CLOCK CYCLE CONTROLLER
  //   contents of eeprom_1 (hex, n*v repeats v):
  //   0,a01,2,3,0,0,f02,e00,0,f02,f02,f02,f02,f02,f02,f02,0,1,2,3,4,6,8,c,10,18,20,30,40,
  //   60,80,c0,100,180,200,29c,300,400,600,6ca,800,fcf,ffe,ffd,ffb,ff7,fef,fdf,e7f,fbf,
  //   f7f,eff,dff,bff,7ff,fff,aaa,555,c00,e00,f00,f80,fe0,ff0,ff8,ffc,7,37,f,1f,3f,7f,ff,
  //   1ff,3ff,fc0,a95,56a,1f8,e07,87,a64,a60,f02,f02,f02,f02,f02,f02,f02,f02,f02,f02,f02,
  //   f02,f02,f02,f02,f02,f02,237,e80,f02,f08,f02,e80,f20,f02,f28,f08,f02,e80,228,f20,f08,
  //   f02,f28,f02,e80,225,f20,f08,f02,f28,f02,e00,e00,f08,a64,e80,222,f20,f08,f02,f28,f02,
  //   e80,220,f20,f08,f02,f28,f02,e80,21e,f20,f08,f02,f28,f02,e80,21c,f20,f08,f02,f28,f02,
  //   e80,21a,f20,f08,f02,f28,f02,e80,218,f20,f08,f02,f28,f02,e80,216,f20,f08,f02,f28,f02,
  //   e80,214,f20,f08,f02,f28,f02,e80,212,f20,f08,f02,f28,f02,e80,211,f20,f08,f02,f28,f02,
  //   e80,236,f48,f02,e80,228,f48,f08,f02,e80,236,f40,f08,f02,e80,228,f40,f02,e80,237,e20,
  //   f20,f02,e80,239,e20,f28,f02,239,e20,f20,f02,e80,238,e20,f28,f02,238,e20,f20,f02,e80,
  //   237,e20,f20,f02,e80,e01,f20,f08,f02,e80,237,e01,f20,f02,e80,241,e01,e01,e01,e01,f20,
  //   f02,e80,e40,e04,f18,f02,e80,e40,e10,228,e04,f18,f08,f02,e80,e40,e04,f10,f08,f02,e80,
  //   e40,e10,228,e04,f10,f02,e80,228,e04,f10,aaa,e40,f18,f02,aae,e10,f10,f02,aa6,e40,f18,
  //   f02,e10,f10,f02,e10,f18,f02,e80,237,f80,f20,f02,e80,f04,e20,f20,f02,e80,e40,e00,f28,
  //   f18,f02,e80,e40,f00,f28,f18,f02,e80,236,228,e20,f20,f02,e80,235,225,e20,f20,f02,e80,
  //   234,222,e20,f20,f02,e80,233,220,e20,f20,f02,e80,232,21e,e20,f20,f02,e80,231,21c,e20,
  //   f20,f02,e80,22f,21a,e20,f20,f02,e80,22e,218,e20,f20,f02,e80,22d,216,e20,f20,f02,e80,
  //   22c,214,e20,f20,f02,e80,22b,212,e20,f20,f02,e80,22a,211,e20,f20,f02,e80,e40,228,228,
  //   f18,f20,f02,e80,e40,23a,225,f18,f20,f02,e80,e40,23b,222,f18,f20,f02,e80,e40,23c,220,
  //   f18,f20,f02,e80,e40,23d,21e,f18,f20,f02,e80,e40,24b,21c,f18,f20,f02,e80,e40,23e,21a,
  //   f18,f20,f02,e80,e40,23f,218,f18,f20,f02,e80,e40,240,216,f18,f20,f02,e80,e40,241,214,
  //   f18,f20,f02,e80,e40,22a,212,f18,f20,f02,e80,e40,237,211,f18,f20,f02,e80,e40,e10,228,
  //   228,f10,f20,f02,e80,e40,236,225,225,e20,f10,f20,f02,e80,e40,235,222,222,e20,f10,f20,
  //   f02,e80,e40,234,220,220,e20,f10,f20,f02,e80,e40,233,21e,21e,e20,f10,f20,f02,e80,e40,
  //   232,21c,21c,e20,f10,f20,f02,e80,e40,231,21a,21a,e20,f10,f20,f02,e80,e40,22f,218,218,
  //   e20,f10,f20,f02,e80,e40,22e,216,216,e20,f10,f20,f02,e80,e40,22d,214,214,e20,f10,f20,
  //   f02,e80,e40,22c,212,212,e20,f10,f20,f02,e80,e40,22b,211,211,e20,f10,f18,f02,e80,e40,
  //   211,213,22c,e20,f10,f20,f02,e80,e40,212,215,22d,e20,f10,f20,f02,e80,e40,214,217,22e,
  //   e20,f10,f20,f02,e80,e40,216,219,22f,e20,f10,f20,f02,e80,e40,218,21b,231,e20,f10,f20,
  //   f02,e80,e40,21a,21d,232,e20,f10,f20,f02,e80,e40,21c,21f,233,e20,f10,f20,f02,e80,e40,
  //   21e,221,234,e20,f10,f20,f02,e80,e40,220,224,235,e20,f10,f20,f02,e80,e40,222,226,236,
  //   e20,f10,f20,f02,e80,e40,225,23a,f18,f20,f02,e80,e40,237,211,f18,f20,f02,e80,e40,213,
  //   213,240,211,e20,f10,f20,f02,e80,e40,215,215,23f,213,e20,f10,f20,f02,e80,e40,217,217,
  //   23e,242,e20,f10,f20,f02,e80,e40,219,219,229,e20,f10,f20,f02,e80,e40,21b,21b,23d,245,
  //   e20,f10,f20,f02,e80,e40,21d,21d,23c,246,e20,f10,f20,f02,e80,e40,21f,21f,230,e20,f10,
  //   f20,f02,e80,e40,221,221,23a,248,e20,f10,f20,f02,e80,e40,224,224,228,249,e20,f10,f20,
  //   f02,e80,e40,226,226,24a,e20,f10,f20,f02,e80,e40,23a,23a,236,e20,f18,f20,f02,e80,e40,
  //   237,237,211,e20,f18,f20,f02,e80,e40,211,e08,f10,f02,e80,e40,210,e08,f20,f02,e80,e40,
  //   210,e08,f18,f02,e80,e40,e10,210,e08,f18,f02,e80,e40,e10,237,e08,e20,f20,f02,e80,e40,
  //   e10,210,e08,236,e20,f28,f18,f02,e80,e40,228,e08,235,e20,f28,f18,f02,e80,e40,225,e08,
  //   234,e20,f28,f18,f02,e80,e40,222,e08,233,e20,f28,f18,f02,e80,e40,220,e08,232,e20,f28,
  //   f18,f02,e80,e40,21e,e08,231,e20,f28,f18,f02,e80,e40,21c,e08,22f,e20,f28,f18,f02,e80,
  //   e40,21a,e08,22e,e20,f28,f18,f02,e80,e40,218,e08,22d,e20,f28,f18,f02,e80,e40,216,e08,
  //   22c,e20,f28,f18,f02,e80,e40,214,e08,22b,e20,f28,f18,f02,e80,e40,212,e08,22a,e20,f28,
  //   f18,f02,e80,e40,211,e08,237,e20,f28,f10,f02,e80,e40,212,e0a,f10,f02,e80,e40,210,e0a,
  //   f20,f02,e80,e40,210,e0a,f18,f02,e80,e40,e10,210,e0a,f18,f02,e80,e40,e10,237,e0a,e20,
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  //   KRB
  //   CML
  //   ISZ
  //   RAMDATA
  //   TFL
  //   IAC
  //   DCA
  //   TSF
  //   RAR
  //   RTR
  //   JMS
  //   TCF
  //   RAL
  //   JMP
  //   IOT
  //   SEQ OPR 1 MICROCODES
  //   ------------------------------------
  //   1 CLA CLL
  //   2 CMA CML
  //   3 IAC
  //   4 RAR RAL RTR RTL BSW
  //   TPC
  //   TSK
  //   RTL
  //   OPR
  //   OSR
  //   TLS
  //   SKP
  //   DIR
  //   ROTATES
  //   SZA
  //   SMA
  //   SPA
  //   AUTO
  //   IND
  //   SNA
  //   CURR
  //   PAGE
  //   SWITCHES
  //   INDOUT
  //   SZL
  //   SNL
  //   HLT
  //   LATCHED
  //   DATA
  //   F
  //   S
  //   LATCHED PC
  //   L
  //   STEP
  //   PHASE
  //   AUTOINDEX
  //   INDIRECT
  //   AND
  //   STEP1
  //   FETCH OP &
  //   INCREMENT PC
  //   SKIP LOGIC
  //   AC=0
  //   AC negative
  //   LINK<>0
  //   IND
  //   STEP1
  //   IND
  //   STEP2
  //   AND
  //   STEP2
  //   AND i
  //   SEQ OPR 2 MICROCODES
  //   ------------------------------------
  //   1 SMA SPA SZA SZN SNK SZL SKP
  //   2 CLA
  //   3 OSR
  //   4 HLT
  //   SMA      7500  skip on minus AC
  //   SPA      7510  skip on plus AC
  //   SZA      7440  skip on zero AC
  //   SNA      7450  skip on non-zero AC
  //   SNL      7420  skip on non-zero link
  //   SZL      7430  skip on zero link
  //   AND-i-auto
  //   iAuto 1
  //   iAuto 2
  //   iAuto 3
  //   TAD
  //   STEP1
  //   TAD
  //   STEP2
  //   CONSOLE
  //   TTY/KBD
  //   -
  //   TAD i
  //   TAD-i-auto
  //   Get address
  //   of M
  //   Save value
  //   from M
  //   indo LATDAT
  //   SKIP IF
  //   AC=ZERO
  //   ISZ i
  //   Save value
  //   from IND
  //   indo LATDAT
  //   ISZ-i-auto
  //   DCA i
  //   DCA-i-auto
  //   Prepare to store
  //   return address
  //   Actually store
  //   return address
  //   Actually increment
  //   PC
  //   Actually set
  //   PC
  //   Pause to accept
  //   new PC inc clk
  //   Prepate to store 
  //   return addr
  //   to [ind]
  //   Store return addr
  //   to [ind]
  //   JMS i
  //   JMS i-auto
  //   Prepare to set
  //   new PC
  //   Actually set
  //   new PC
  //   Prepare to set PC
  //   with new vector
  //   JMP i
  //   JMP i-auto
  //   OPR 1
  //   OPR 2
  //   OPR 3
  //   IOT DECODER
  //   IR DECODER
  //   OPR DECODER
endmodule
